// Logisim project MarcosMartim.circ as structural Verilog
module meiosomador (
  input  A,
  input  B,
  output Soma,
  output Cout
);

  wire and_1_out, and_2_out, not_1_out, not_2_out;

  not not_1 (not_1_out, A);
  not not_2 (not_2_out, B);
  and and_1 (and_1_out, not_1_out, B);
  and and_2 (and_2_out, A, not_2_out);
  and and_3 (Cout, A, B);
  or or_1 (Soma, and_1_out, and_2_out);
endmodule

module somador (
  input  A,
  input  B,
  input  Cin,
  output Soma,
  output Cout
);

  wire and_1_out, and_2_out, and_3_out, and_4_out, and_5_out, and_6_out, and_7_out, not_1_out, not_2_out,
       not_3_out;

  not not_1 (not_1_out, A);
  not not_2 (not_2_out, B);
  not not_3 (not_3_out, Cin);
  and and_1 (and_1_out, not_1_out, not_2_out, Cin);
  and and_2 (and_2_out, not_1_out, B, not_3_out);
  and and_3 (and_3_out, A, not_2_out, not_3_out);
  and and_4 (and_4_out, A, B, Cin);
  and and_5 (and_5_out, B, Cin);
  and and_6 (and_6_out, A, Cin);
  and and_7 (and_7_out, A, B);
  or or_1 (Soma, and_1_out, and_2_out, and_3_out, and_4_out);
  or or_2 (Cout, and_5_out, and_6_out, and_7_out);
endmodule

module doismeios (
  input  A,
  input  B,
  input  Ci,
  output out_4,
  output out_5
);

  wire meiosomador_1_cout, meiosomador_1_soma, meiosomador_2_cout;

  meiosomador meiosomador_1 (.A(A), .B(B), .Soma(meiosomador_1_soma), .Cout(meiosomador_1_cout));
  meiosomador meiosomador_2 (.A(meiosomador_1_soma), .B(Ci), .Soma(out_4), .Cout(meiosomador_2_cout));
  or or_1 (out_5, meiosomador_1_cout, meiosomador_2_cout);
endmodule

module somadorcascata (
  input  in_1,
  input  in_2,
  input  in_3,
  input  in_4,
  input  in_5,
  input  in_6,
  input  in_7,
  input  in_8,
  input  in_9,
  input  in_10,
  input  in_11,
  input  in_12,
  input  in_13,
  input  in_14,
  input  in_15,
  input  in_16,
  output out_17,
  output out_18,
  output out_19,
  output out_20,
  output out_21,
  output out_22,
  output out_23,
  output out_24,
  output out_25
);

  wire doismeios_1_out_5, doismeios_2_out_5, doismeios_3_out_5, doismeios_4_out_5, doismeios_5_out_5,
       doismeios_6_out_5, doismeios_7_out_5;

  doismeios doismeios_1 (.A(in_1), .B(in_2), .out_4(out_17), .out_5(doismeios_1_out_5));  // open: Ci
  doismeios doismeios_2 (.A(in_3), .B(in_4), .Ci(doismeios_1_out_5), .out_4(out_18), .out_5(doismeios_2_out_5));
  doismeios doismeios_3 (.A(in_5), .B(in_6), .Ci(doismeios_2_out_5), .out_4(out_19), .out_5(doismeios_3_out_5));
  doismeios doismeios_4 (.A(in_7), .B(in_8), .Ci(doismeios_3_out_5), .out_4(out_20), .out_5(doismeios_4_out_5));
  doismeios doismeios_5 (.A(in_9), .B(in_10), .Ci(doismeios_4_out_5), .out_4(out_21), .out_5(doismeios_5_out_5));
  doismeios doismeios_6 (.A(in_11), .B(in_12), .Ci(doismeios_5_out_5), .out_4(out_22), .out_5(doismeios_6_out_5));
  doismeios doismeios_7 (.A(in_13), .B(in_14), .Ci(doismeios_6_out_5), .out_4(out_23), .out_5(doismeios_7_out_5));
  doismeios doismeios_8 (.A(in_15), .B(in_16), .Ci(doismeios_7_out_5), .out_4(out_24), .out_5(out_25));
endmodule

module Somas (
  input  in_1,
  input  in_2,
  input  in_3,
  input  in_4,
  input  in_5,
  input  in_6,
  input  in_7,
  input  in_8,
  input  in_9,
  input  in_10,
  input  in_11,
  input  in_12,
  input  in_13,
  input  in_14,
  input  in_15,
  input  in_16,
  output out_17,
  output out_18,
  output out_19,
  output out_20,
  output out_21,
  output out_22,
  output out_23,
  output out_24,
  output Cout
);

  somadorcascata somadorcascata_1 (
    .in_1(in_1), .in_2(in_2), .in_3(in_3), .in_4(in_4), .in_5(in_5), .in_6(in_6), .in_7(in_7), .in_8(in_8),
    .in_9(in_9), .in_10(in_10), .in_11(in_11), .in_12(in_12), .in_13(in_13), .in_14(in_14), .in_15(in_15),
    .in_16(in_16), .out_17(out_17), .out_18(out_18), .out_19(out_19), .out_20(out_20), .out_21(out_21),
    .out_22(out_22), .out_23(out_23), .out_24(out_24), .out_25(Cout));
endmodule

module comparador1 (
  input  A,
  input  B,
  output Q1,
  output Q2,
  output Q3
);

  wire and_1_out, and_2_out, not_1_out, not_2_out;

  not not_1 (not_1_out, A);
  not not_2 (not_2_out, B);
  and and_1 (and_1_out, not_1_out, not_2_out);
  and and_2 (and_2_out, A, B);
  and and_3 (Q2, A, not_2_out);
  and and_4 (Q3, not_1_out, B);
  or or_1 (Q1, and_1_out, and_2_out);

  // Notes on the sheet:
  //   AigualB
  //   AmaiorB
  //   AmenorB
endmodule

module shift_direita (
  input  SEMPRE0,
  input  [3:0] in_2,
  input  shift_dir,
  input  CLK,
  output out_5,
  output out_6,
  output out_7,
  output saida_util
);

  wire multiplexer_1_out, multiplexer_2_out, multiplexer_3_out, multiplexer_4_out;

  Multiplexer #(.enable("false")) multiplexer_1 (
    .in0(in_2[3]), .in1(SEMPRE0), .out(multiplexer_1_out), .sel(shift_dir));
  Multiplexer #(.enable("false")) multiplexer_2 (.in0(in_2[2]), .in1(out_5), .out(multiplexer_2_out), .sel(shift_dir));
  Multiplexer #(.enable("false")) multiplexer_3 (.in0(in_2[1]), .in1(out_6), .out(multiplexer_3_out), .sel(shift_dir));
  Multiplexer #(.enable("false")) multiplexer_4 (.in0(in_2[0]), .in1(out_7), .out(multiplexer_4_out), .sel(shift_dir));
  D_Flip_Flop d_ff_1 (.D(multiplexer_1_out), .clk(CLK), .Q(out_5));  // open: Qn, preset, reset
  D_Flip_Flop d_ff_2 (.D(multiplexer_2_out), .clk(CLK), .Q(out_6));  // open: Qn, preset, reset
  D_Flip_Flop d_ff_3 (.D(multiplexer_3_out), .clk(CLK), .Q(out_7));  // open: Qn, preset, reset
  D_Flip_Flop d_ff_4 (.D(multiplexer_4_out), .clk(CLK), .Q(saida_util));  // open: Qn, preset, reset
endmodule

module MULTIPLICAR (
  input  in_1,
  input  [3:0] in_2,
  input  in_3,
  input  [7:0] in_4,
  input  in_5,
  input  in_6,
  input  [7:0] in_7,
  input  in_8,
  output out_9,
  output out_10,
  output out_11,
  output out_12,
  output [7:0] out_13,
  output [7:0] out_14,
  output [7:0] out_15,
  output out_16,
  output [7:0] out_17
);

  wire clock_1_out, clock_2_out, clock_3_out, clock_4_out, clock_5_out, clock_6_out, clock_7_out,
       clock_8_out, clock_9_out, clock_10_out;

  Clock clock_1 (.out(clock_1_out));
  D_Flip_Flop d_ff_1 (.D(out_15[0]), .clk(clock_2_out), .Q(out_17[0]), .reset(in_8));  // open: Qn, preset
  Clock clock_2 (.out(clock_2_out));
  Adder adder_1 (.a(out_14), .b(out_17), .out(out_15), .cout(out_16));  // open: cin
  D_Flip_Flop d_ff_2 (.D(out_15[1]), .clk(clock_3_out), .Q(out_17[1]), .reset(in_8));  // open: Qn, preset
  Clock clock_3 (.out(clock_3_out));
  shif_esquerda shif_esquerda_1 (.I(in_4), .sempre0(in_5), .shift_esq(in_6), .clk(clock_1_out), .S(out_13));
  D_Flip_Flop d_ff_3 (.D(out_15[2]), .clk(clock_4_out), .Q(out_17[2]), .reset(in_8));  // open: Qn, preset
  Clock clock_4 (.out(clock_4_out));
  Multiplexer #(.enable("false"), .width(8)) multiplexer_1 (.in0(in_7), .in1(out_13), .out(out_14), .sel(out_12));
  D_Flip_Flop d_ff_4 (.D(out_15[3]), .clk(clock_5_out), .Q(out_17[3]), .reset(in_8));  // open: Qn, preset
  Clock clock_5 (.out(clock_5_out));
  Clock clock_6 (.out(clock_6_out));
  D_Flip_Flop d_ff_5 (.D(out_15[4]), .clk(clock_6_out), .Q(out_17[4]), .reset(in_8));  // open: Qn, preset
  Clock clock_7 (.out(clock_7_out));
  D_Flip_Flop d_ff_6 (.D(out_15[5]), .clk(clock_8_out), .Q(out_17[5]), .reset(in_8));  // open: Qn, preset
  Clock clock_8 (.out(clock_8_out));
  D_Flip_Flop d_ff_7 (.D(out_15[6]), .clk(clock_9_out), .Q(out_17[6]), .reset(in_8));  // open: Qn, preset
  Clock clock_9 (.out(clock_9_out));
  D_Flip_Flop d_ff_8 (.D(out_15[7]), .clk(clock_10_out), .Q(out_17[7]), .reset(in_8));  // open: Qn, preset
  Clock clock_10 (.out(clock_10_out));
  shift_direita shift_direita_1 (
    .SEMPRE0(in_1), .in_2(in_2), .shift_dir(in_3), .CLK(clock_7_out), .out_5(out_9), .out_6(out_10),
    .out_7(out_11), .saida_util(out_12));
endmodule

module shif_esquerda (
  input  [7:0] I,
  input  sempre0,
  input  shift_esq,
  input  clk,
  output [7:0] S
);

  wire multiplexer_1_out, multiplexer_2_out, multiplexer_3_out, multiplexer_4_out, multiplexer_5_out,
       multiplexer_6_out, multiplexer_7_out, multiplexer_8_out;

  Multiplexer #(.enable("false")) multiplexer_1 (.in0(I[7]), .in1(S[6]), .out(multiplexer_1_out), .sel(shift_esq));
  Multiplexer #(.enable("false")) multiplexer_2 (.in0(I[6]), .in1(S[5]), .out(multiplexer_2_out), .sel(shift_esq));
  Multiplexer #(.enable("false")) multiplexer_3 (.in0(I[5]), .in1(S[4]), .out(multiplexer_3_out), .sel(shift_esq));
  Multiplexer #(.enable("false")) multiplexer_4 (.in0(I[4]), .in1(S[3]), .out(multiplexer_4_out), .sel(shift_esq));
  Multiplexer #(.enable("false")) multiplexer_5 (.in0(I[3]), .in1(S[2]), .out(multiplexer_5_out), .sel(shift_esq));
  Multiplexer #(.enable("false")) multiplexer_6 (.in0(I[2]), .in1(S[1]), .out(multiplexer_6_out), .sel(shift_esq));
  Multiplexer #(.enable("false")) multiplexer_7 (.in0(I[1]), .in1(S[0]), .out(multiplexer_7_out), .sel(shift_esq));
  Multiplexer #(.enable("false")) multiplexer_8 (.in0(I[0]), .in1(sempre0), .out(multiplexer_8_out), .sel(shift_esq));
  D_Flip_Flop d_ff_1 (.D(multiplexer_1_out), .clk(clk), .Q(S[7]));  // open: Qn, preset, reset
  D_Flip_Flop d_ff_2 (.D(multiplexer_2_out), .clk(clk), .Q(S[6]));  // open: Qn, preset, reset
  D_Flip_Flop d_ff_3 (.D(multiplexer_3_out), .clk(clk), .Q(S[5]));  // open: Qn, preset, reset
  D_Flip_Flop d_ff_4 (.D(multiplexer_4_out), .clk(clk), .Q(S[4]));  // open: Qn, preset, reset
  D_Flip_Flop d_ff_5 (.D(multiplexer_5_out), .clk(clk), .Q(S[3]));  // open: Qn, preset, reset
  D_Flip_Flop d_ff_6 (.D(multiplexer_6_out), .clk(clk), .Q(S[2]));  // open: Qn, preset, reset
  D_Flip_Flop d_ff_7 (.D(multiplexer_7_out), .clk(clk), .Q(S[1]));  // open: Qn, preset, reset
  D_Flip_Flop d_ff_8 (.D(multiplexer_8_out), .clk(clk), .Q(S[0]));  // open: Qn, preset, reset
endmodule
