// Logisim project BrunoMartins_AfonsoAlmeidaTB7.circ as structural Verilog
module Shift_Esquerda (
  input  [7:0] cando,
  input  Shift_Esq,
  output [7:0] out_3
);

  wire clock_1_out, multiplexer_1_out, multiplexer_2_out, multiplexer_3_out, multiplexer_4_out,
       multiplexer_5_out, multiplexer_6_out, multiplexer_7_out, multiplexer_8_out;

  Multiplexer #(.enable("false")) multiplexer_1 (
    .in0(cando[0]), .in1(out_3[1]), .out(multiplexer_1_out), .sel(Shift_Esq));
  Multiplexer #(.enable("false")) multiplexer_2 (
    .in0(cando[1]), .in1(out_3[2]), .out(multiplexer_2_out), .sel(Shift_Esq));
  Multiplexer #(.enable("false")) multiplexer_3 (
    .in0(cando[2]), .in1(out_3[3]), .out(multiplexer_3_out), .sel(Shift_Esq));
  Multiplexer #(.enable("false")) multiplexer_4 (
    .in0(cando[3]), .in1(out_3[4]), .out(multiplexer_4_out), .sel(Shift_Esq));
  Multiplexer #(.enable("false")) multiplexer_5 (
    .in0(cando[4]), .in1(out_3[5]), .out(multiplexer_5_out), .sel(Shift_Esq));
  Multiplexer #(.enable("false")) multiplexer_6 (
    .in0(cando[5]), .in1(out_3[6]), .out(multiplexer_6_out), .sel(Shift_Esq));
  Multiplexer #(.enable("false")) multiplexer_7 (
    .in0(cando[6]), .in1(out_3[7]), .out(multiplexer_7_out), .sel(Shift_Esq));
  Multiplexer #(.enable("false")) multiplexer_8 (.in0(cando[7]), .in1(1'b0), .out(multiplexer_8_out), .sel(Shift_Esq));
  Clock clock_1 (.out(clock_1_out));
  D_Flip_Flop d_ff_1 (.D(multiplexer_1_out), .clk(clock_1_out), .Q(out_3[0]));  // open: Qn, preset, reset
  D_Flip_Flop d_ff_2 (.D(multiplexer_2_out), .clk(clock_1_out), .Q(out_3[1]));  // open: Qn, preset, reset
  D_Flip_Flop d_ff_3 (.D(multiplexer_3_out), .clk(clock_1_out), .Q(out_3[2]));  // open: Qn, preset, reset
  D_Flip_Flop d_ff_4 (.D(multiplexer_4_out), .clk(clock_1_out), .Q(out_3[3]));  // open: Qn, preset, reset
  D_Flip_Flop d_ff_5 (.D(multiplexer_5_out), .clk(clock_1_out), .Q(out_3[4]));  // open: Qn, preset, reset
  D_Flip_Flop d_ff_6 (.D(multiplexer_6_out), .clk(clock_1_out), .Q(out_3[5]));  // open: Qn, preset, reset
  D_Flip_Flop d_ff_7 (.D(multiplexer_7_out), .clk(clock_1_out), .Q(out_3[6]));  // open: Qn, preset, reset
  D_Flip_Flop d_ff_8 (.D(multiplexer_8_out), .clk(clock_1_out), .Q(out_3[7]));  // open: Qn, preset, reset
endmodule

module Shift_Direita (
  input  [3:0] cador,
  input  Shift_Dir,
  output [3:0] out_3
);

  wire clock_1_out, multiplexer_1_out, multiplexer_2_out, multiplexer_3_out, multiplexer_4_out;

  Multiplexer #(.enable("false")) multiplexer_1 (.in0(cador[0]), .in1(1'b0), .out(multiplexer_1_out), .sel(Shift_Dir));
  Multiplexer #(.enable("false")) multiplexer_2 (
    .in0(cador[1]), .in1(out_3[0]), .out(multiplexer_2_out), .sel(Shift_Dir));
  Multiplexer #(.enable("false")) multiplexer_3 (
    .in0(cador[2]), .in1(out_3[1]), .out(multiplexer_3_out), .sel(Shift_Dir));
  Multiplexer #(.enable("false")) multiplexer_4 (
    .in0(cador[3]), .in1(out_3[2]), .out(multiplexer_4_out), .sel(Shift_Dir));
  Clock clock_1 (.out(clock_1_out));
  D_Flip_Flop d_ff_1 (.D(multiplexer_1_out), .clk(clock_1_out), .Q(out_3[0]));  // open: Qn, preset, reset
  D_Flip_Flop d_ff_2 (.D(multiplexer_2_out), .clk(clock_1_out), .Q(out_3[1]));  // open: Qn, preset, reset
  D_Flip_Flop d_ff_3 (.D(multiplexer_3_out), .clk(clock_1_out), .Q(out_3[2]));  // open: Qn, preset, reset
  D_Flip_Flop d_ff_4 (.D(multiplexer_4_out), .clk(clock_1_out), .Q(out_3[3]));  // open: Qn, preset, reset
endmodule

module Multiplicador (
  input  [7:0] in_1,
  input  in_2,
  input  in_3,
  input  [3:0] in_4,
  output [3:0] out_5
);

  wire clock_1_out, undriven;
  wire [7:0] adder_1_out, multiplexer_1_out, Qout, shift_esquerda_1_out_3;

  Shift_Esquerda shift_esquerda_1 (.cando(in_1), .Shift_Esq(undriven), .out_3(shift_esquerda_1_out_3));
  Shift_Direita shift_direita_1 (.cador(in_4), .out_3(out_5));  // open: Shift_Dir
  Multiplexer #(.enable("false"), .width(8)) multiplexer_1 (
    .in0(Qout), .in1(shift_esquerda_1_out_3), .out(multiplexer_1_out), .sel(in_2));
  Adder adder_1 (.a(multiplexer_1_out), .b(Qout), .out(adder_1_out));  // open: cin, cout
  Clock clock_1 (.out(clock_1_out));
  Register register_1 (.D(adder_1_out), .en(1'b1), .clk(clock_1_out), .Q(Qout), .clr(in_3));
  // Probe on Qout
endmodule
