// Logisim project Circuitocontador.circ as structural Verilog: 4 circuits, main circuit Main1
module Main1 (
  input  in_1,
  input  in_2,
  input  in_3,
  input  in_4,
  input  A,
  input  B,
  input  C,
  input  D
);

  wire c74ls163_1_q0, c74ls163_1_q1, c74ls163_1_q2, c74ls163_1_q3, clock_1_out, descodificador_1_p5,
       descodificador_1_p6, descodificador_1_p7, descodificador_1_p8, descodificador_1_p9,
       descodificador_1_p10, descodificador_1_p11;

  Clock clock_1 (.out(clock_1_out));
  C74ls163 c74ls163_1 (
    .ENP(in_1), .ENT(in_2), .LOAD_N(in_3), .CLEAR_N(in_4), .CLK(clock_1_out), .A(A), .B(B), .C(C), .D(D),
    .Q0(c74ls163_1_q0), .Q1(c74ls163_1_q1), .Q2(c74ls163_1_q2), .Q3(c74ls163_1_q3));  // open: CO
  // descodificador descodificador_1: pin names not known; wires that end beside it: c74ls163_1_q3, c74ls163_1_q2, c74ls163_1_q1, c74ls163_1_q0, descodificador_1_p5, descodificador_1_p6, descodificador_1_p7, descodificador_1_p8, descodificador_1_p9, descodificador_1_p10, descodificador_1_p11
  _7_Segment_Display u_7_segment_display_1 (
    .g(descodificador_1_p11), .f(descodificador_1_p10), .a(descodificador_1_p5), .b(descodificador_1_p6),
    .e(descodificador_1_p9), .d(descodificador_1_p8), .c(descodificador_1_p7));  // open: dp
endmodule

module Main2 (
  input  in_1,
  input  in_2,
  input  in_3,
  input  in_4,
  input  A,
  input  B,
  input  C,
  input  D
);

  wire clock_1_out;

  Clock clock_1 (.out(clock_1_out));
  C74ls163 c74ls163_1 (
    .ENP(in_1), .ENT(in_2), .LOAD_N(in_3), .CLEAR_N(in_4), .CLK(clock_1_out), .A(A), .B(B), .C(C), .D(D));  // open: CO, Q0, Q1, Q2, Q3
endmodule

module Main3 (
  input  in_1,
  input  in_2,
  input  in_3,
  input  A,
  input  B,
  input  C,
  input  D
);

  wire c74ls163_1_q0, c74ls163_1_q1, c74ls163_1_q2, c74ls163_1_q3, clock_1_out, descodificador_1_p5,
       descodificador_1_p6, descodificador_1_p7, descodificador_1_p8, descodificador_1_p9,
       descodificador_1_p10, descodificador_1_p11, nand_1_out;

  Clock clock_1 (.out(clock_1_out));
  nand nand_1 (nand_1_out, c74ls163_1_q3, c74ls163_1_q0);
  C74ls163 c74ls163_1 (
    .ENP(in_1), .ENT(in_2), .LOAD_N(nand_1_out), .CLEAR_N(in_3), .CLK(clock_1_out), .A(A), .B(B), .C(C),
    .D(D), .Q0(c74ls163_1_q0), .Q1(c74ls163_1_q1), .Q2(c74ls163_1_q2), .Q3(c74ls163_1_q3));  // open: CO
  // NOT_Gate not_1 has open pins: in=c74ls163_1_q2, out=open
  // NOT_Gate not_2 has open pins: in=c74ls163_1_q1, out=open
  // descodificador descodificador_1: pin names not known; wires that end beside it: c74ls163_1_q3, c74ls163_1_q2, c74ls163_1_q1, c74ls163_1_q0, descodificador_1_p5, descodificador_1_p6, descodificador_1_p7, descodificador_1_p8, descodificador_1_p9, descodificador_1_p10, descodificador_1_p11
  _7_Segment_Display u_7_segment_display_1 (
    .g(descodificador_1_p11), .f(descodificador_1_p10), .a(descodificador_1_p5), .b(descodificador_1_p6),
    .e(descodificador_1_p9), .d(descodificador_1_p8), .c(descodificador_1_p7));  // open: dp
endmodule

module Contador2 (
  input  in_1,
  input  in_2,
  input  in_3,
  input  in_4,
  input  A,
  input  B,
  input  C,
  input  D
);

  wire clock_1_out;

  Clock clock_1 (.out(clock_1_out));
  C74ls163 c74ls163_1 (
    .ENP(in_1), .ENT(in_2), .LOAD_N(in_3), .CLEAR_N(in_4), .CLK(clock_1_out), .A(A), .B(B), .C(C), .D(D));  // open: CO, Q0, Q1, Q2, Q3
  // C74ls163 c74ls163_2: pin names not known
endmodule
