// Logisim project Rafael_Sousa.circ as structural Verilog: 1 circuit, main circuit Des_4bit
module Des_4bit (
  input  X3,
  input  X2,
  input  X1,
  input  X0,
  output Y0,
  output Y1,
  output Y2,
  output Y3,
  output Y4,
  output Y5,
  output Y6,
  output Y7,
  output Y8,
  output Y9
);

  wire not_1_out, not_2_out, not_3_out, not_4_out;

  not not_1 (not_1_out, X3);
  not not_2 (not_2_out, X2);
  not not_3 (not_3_out, X1);
  not not_4 (not_4_out, X0);
  and and_1 (Y0, not_1_out, not_2_out, not_3_out, not_4_out);
  and and_2 (Y1, not_1_out, not_2_out, not_3_out, X0);
  and and_3 (Y2, not_1_out, not_2_out, X1, not_4_out);
  and and_4 (Y3, not_1_out, not_2_out, X1, X0);
  and and_5 (Y4, not_1_out, X2, not_3_out, not_4_out);
  and and_6 (Y5, not_1_out, X2, not_3_out, X0);
  and and_7 (Y6, not_1_out, X2, X1, not_4_out);
  and and_8 (Y7, not_1_out, X2, X1, X0);
  and and_9 (Y8, X3, not_2_out, not_3_out, not_4_out);
  and and_10 (Y9, X3, not_2_out, not_3_out, X0);
endmodule
