// Logisim project SDT7.circ as structural Verilog
module meiosomador (
  input  A,
  input  B,
  output Soma,
  output Cout
);

  wire and_1_out, and_2_out, not_1_out, not_2_out;

  not not_1 (not_1_out, A);
  not not_2 (not_2_out, B);
  and and_1 (and_1_out, not_1_out, B);
  and and_2 (and_2_out, A, not_2_out);
  and and_3 (Cout, A, B);
  or or_1 (Soma, and_1_out, and_2_out);
endmodule

module somador (
  input  A,
  input  B,
  input  Cin,
  output Soma,
  output Cout
);

  wire and_1_out, and_2_out, and_3_out, and_4_out, and_5_out, and_6_out, and_7_out, not_1_out, not_2_out,
       not_3_out;

  not not_1 (not_1_out, A);
  not not_2 (not_2_out, B);
  not not_3 (not_3_out, Cin);
  and and_1 (and_1_out, not_1_out, not_2_out, Cin);
  and and_2 (and_2_out, not_1_out, B, not_3_out);
  and and_3 (and_3_out, A, not_2_out, not_3_out);
  and and_4 (and_4_out, A, B, Cin);
  and and_5 (and_5_out, B, Cin);
  and and_6 (and_6_out, A, Cin);
  and and_7 (and_7_out, A, B);
  or or_1 (Soma, and_1_out, and_2_out, and_3_out, and_4_out);
  or or_2 (Cout, and_5_out, and_6_out, and_7_out);
endmodule

module doismeios (
  input  A,
  input  B,
  input  Ci,
  output out_4,
  output out_5
);

  wire meiosomador_1_cout, meiosomador_1_soma, meiosomador_2_cout;

  meiosomador meiosomador_1 (.A(A), .B(B), .Soma(meiosomador_1_soma), .Cout(meiosomador_1_cout));
  meiosomador meiosomador_2 (.A(meiosomador_1_soma), .B(Ci), .Soma(out_4), .Cout(meiosomador_2_cout));
  or or_1 (out_5, meiosomador_1_cout, meiosomador_2_cout);
endmodule

module somadorcascata (
  input  in_1,
  input  in_2,
  input  in_3,
  input  in_4,
  input  in_5,
  input  in_6,
  input  in_7,
  input  in_8,
  input  in_9,
  input  in_10,
  input  in_11,
  input  in_12,
  input  in_13,
  input  in_14,
  input  in_15,
  input  in_16,
  output out_17,
  output out_18,
  output out_19,
  output out_20,
  output out_21,
  output out_22,
  output out_23,
  output out_24,
  output out_25
);

  wire doismeios_1_out_5, doismeios_2_out_5, doismeios_3_out_5, doismeios_4_out_5, doismeios_5_out_5,
       doismeios_6_out_5, doismeios_7_out_5;

  doismeios doismeios_1 (.A(in_1), .B(in_2), .out_4(out_17), .out_5(doismeios_1_out_5));  // open: Ci
  doismeios doismeios_2 (.A(in_3), .B(in_4), .Ci(doismeios_1_out_5), .out_4(out_18), .out_5(doismeios_2_out_5));
  doismeios doismeios_3 (.A(in_5), .B(in_6), .Ci(doismeios_2_out_5), .out_4(out_19), .out_5(doismeios_3_out_5));
  doismeios doismeios_4 (.A(in_7), .B(in_8), .Ci(doismeios_3_out_5), .out_4(out_20), .out_5(doismeios_4_out_5));
  doismeios doismeios_5 (.A(in_9), .B(in_10), .Ci(doismeios_4_out_5), .out_4(out_21), .out_5(doismeios_5_out_5));
  doismeios doismeios_6 (.A(in_11), .B(in_12), .Ci(doismeios_5_out_5), .out_4(out_22), .out_5(doismeios_6_out_5));
  doismeios doismeios_7 (.A(in_13), .B(in_14), .Ci(doismeios_6_out_5), .out_4(out_23), .out_5(doismeios_7_out_5));
  doismeios doismeios_8 (.A(in_15), .B(in_16), .Ci(doismeios_7_out_5), .out_4(out_24), .out_5(out_25));
endmodule

module Somas (
  input  in_1,
  input  in_2,
  input  in_3,
  input  in_4,
  input  in_5,
  input  in_6,
  input  in_7,
  input  in_8,
  input  in_9,
  input  in_10,
  input  in_11,
  input  in_12,
  input  in_13,
  input  in_14,
  input  in_15,
  input  in_16,
  output out_17,
  output out_18,
  output out_19,
  output out_20,
  output out_21,
  output out_22,
  output out_23,
  output out_24,
  output Cout
);

  somadorcascata somadorcascata_1 (
    .in_1(in_1), .in_2(in_2), .in_3(in_3), .in_4(in_4), .in_5(in_5), .in_6(in_6), .in_7(in_7), .in_8(in_8),
    .in_9(in_9), .in_10(in_10), .in_11(in_11), .in_12(in_12), .in_13(in_13), .in_14(in_14), .in_15(in_15),
    .in_16(in_16), .out_17(out_17), .out_18(out_18), .out_19(out_19), .out_20(out_20), .out_21(out_21),
    .out_22(out_22), .out_23(out_23), .out_24(out_24), .out_25(Cout));
endmodule

module comparador1 (
  input  A,
  input  B,
  output Q1,
  output Q2,
  output Q3
);

  wire and_1_out, and_2_out, not_1_out, not_2_out;

  not not_1 (not_1_out, A);
  not not_2 (not_2_out, B);
  and and_1 (and_1_out, not_1_out, not_2_out);
  and and_2 (and_2_out, A, B);
  and and_3 (Q2, A, not_2_out);
  and and_4 (Q3, not_1_out, B);
  or or_1 (Q1, and_1_out, and_2_out);

  // Notes on the sheet:
  //   AigualB
  //   AmaiorB
  //   AmenorB
endmodule

module shift_direita (
  input  i3,
  input  SEMPRE0,
  input  i2,
  input  i1,
  input  i0,
  input  shift_dir,
  input  CLK,
  output out_8,
  output out_9,
  output out_10,
  output saida_util
);

  wire multiplexer_1_out, multiplexer_2_out, multiplexer_3_out, multiplexer_4_out;

  Multiplexer #(.enable("false")) multiplexer_1 (.in0(i3), .in1(SEMPRE0), .out(multiplexer_1_out), .sel(shift_dir));
  Multiplexer #(.enable("false")) multiplexer_2 (.in0(i2), .in1(out_8), .out(multiplexer_2_out), .sel(shift_dir));
  Multiplexer #(.enable("false")) multiplexer_3 (.in0(i1), .in1(out_9), .out(multiplexer_3_out), .sel(shift_dir));
  Multiplexer #(.enable("false")) multiplexer_4 (.in0(i0), .in1(out_10), .out(multiplexer_4_out), .sel(shift_dir));
  D_Flip_Flop d_ff_1 (.D(multiplexer_1_out), .clk(CLK), .Q(out_8));  // open: Qn, preset, reset
  D_Flip_Flop d_ff_2 (.D(multiplexer_2_out), .clk(CLK), .Q(out_9));  // open: Qn, preset, reset
  D_Flip_Flop d_ff_3 (.D(multiplexer_3_out), .clk(CLK), .Q(out_10));  // open: Qn, preset, reset
  D_Flip_Flop d_ff_4 (.D(multiplexer_4_out), .clk(CLK), .Q(saida_util));  // open: Qn, preset, reset
endmodule

module MULTIPLICAR (
  input  in_1,
  input  in_2,
  input  in_3,
  input  in_4,
  input  in_5,
  input  in_6,
  input  in_7,
  input  in_8,
  input  in_9,
  input  in_10,
  input  in_11,
  input  in_12,
  input  in_13,
  input  in_14,
  input  in_15,
  input  in_16,
  input  in_17,
  output out_18,
  output out_19,
  output out_20,
  output out_21
);

  wire clock_1_out;

  shif_esquerda shif_esquerda_1 (
    .i7(in_3), .i6(in_5), .i5(in_7), .i4(in_9), .i3(in_11), .i2(in_12), .i1(in_13), .i0(in_14),
    .sempre0(in_15), .shift_esq(in_16), .clk(in_17));  // open: s7, s6, s5, s4, s3, s2, s1, s0
  Clock clock_1 (.out(clock_1_out));
  shift_direita shift_direita_1 (
    .i3(in_1), .SEMPRE0(in_2), .i2(in_4), .i1(in_6), .i0(in_8), .shift_dir(in_10), .CLK(clock_1_out),
    .out_8(out_18), .out_9(out_19), .out_10(out_20), .saida_util(out_21));
endmodule

module shif_esquerda (
  input  i7,
  input  i6,
  input  i5,
  input  i4,
  input  i3,
  input  i2,
  input  i1,
  input  i0,
  input  sempre0,
  input  shift_esq,
  input  clk,
  output s7,
  output s6,
  output s5,
  output s4,
  output s3,
  output s2,
  output s1,
  output s0
);

  wire multiplexer_1_out, multiplexer_2_out, multiplexer_3_out, multiplexer_4_out, multiplexer_5_out,
       multiplexer_6_out, multiplexer_7_out, multiplexer_8_out;

  Multiplexer #(.enable("false")) multiplexer_1 (.in0(i7), .in1(s6), .out(multiplexer_1_out), .sel(shift_esq));
  Multiplexer #(.enable("false")) multiplexer_2 (.in0(i6), .in1(s5), .out(multiplexer_2_out), .sel(shift_esq));
  Multiplexer #(.enable("false")) multiplexer_3 (.in0(i5), .in1(s4), .out(multiplexer_3_out), .sel(shift_esq));
  Multiplexer #(.enable("false")) multiplexer_4 (.in0(i4), .in1(s3), .out(multiplexer_4_out), .sel(shift_esq));
  Multiplexer #(.enable("false")) multiplexer_5 (.in0(i3), .in1(s2), .out(multiplexer_5_out), .sel(shift_esq));
  Multiplexer #(.enable("false")) multiplexer_6 (.in0(i2), .in1(s1), .out(multiplexer_6_out), .sel(shift_esq));
  Multiplexer #(.enable("false")) multiplexer_7 (.in0(i1), .in1(s0), .out(multiplexer_7_out), .sel(shift_esq));
  Multiplexer #(.enable("false")) multiplexer_8 (.in0(i0), .in1(sempre0), .out(multiplexer_8_out), .sel(shift_esq));
  D_Flip_Flop d_ff_1 (.D(multiplexer_1_out), .clk(clk), .Q(s7));  // open: Qn, preset, reset
  D_Flip_Flop d_ff_2 (.D(multiplexer_2_out), .clk(clk), .Q(s6));  // open: Qn, preset, reset
  D_Flip_Flop d_ff_3 (.D(multiplexer_3_out), .clk(clk), .Q(s5));  // open: Qn, preset, reset
  D_Flip_Flop d_ff_4 (.D(multiplexer_4_out), .clk(clk), .Q(s4));  // open: Qn, preset, reset
  D_Flip_Flop d_ff_5 (.D(multiplexer_5_out), .clk(clk), .Q(s3));  // open: Qn, preset, reset
  D_Flip_Flop d_ff_6 (.D(multiplexer_6_out), .clk(clk), .Q(s2));  // open: Qn, preset, reset
  D_Flip_Flop d_ff_7 (.D(multiplexer_7_out), .clk(clk), .Q(s1));  // open: Qn, preset, reset
  D_Flip_Flop d_ff_8 (.D(multiplexer_8_out), .clk(clk), .Q(s0));  // open: Qn, preset, reset
endmodule
