// Logisim project SD_RodrigoFerreira_TelmoMachado.circ as structural Verilog
module SG_A (
  input  X,
  input  Y,
  input  Z,
  input  W,
  output a
);

  wire and_1_out, and_2_out, and_3_out, and_4_out, not_1_out, not_2_out, not_3_out, not_4_out;

  not not_1 (not_1_out, Y);
  and and_1 (and_1_out, not_1_out, not_2_out);
  not not_2 (not_2_out, W);
  not not_3 (not_3_out, X);
  and and_2 (and_2_out, not_3_out, Z);
  and and_3 (and_3_out, Y, W);
  and and_4 (and_4_out, X, not_4_out);
  not not_4 (not_4_out, Z);
  or or_1 (a, and_1_out, and_2_out, and_3_out, and_4_out);
endmodule

module SG_B (
  input  X,
  input  Y,
  input  Z,
  input  W,
  output b
);

  wire and_1_out, and_2_out, and_3_out, and_4_out, not_1_out, not_2_out, not_3_out, not_4_out;

  not not_1 (not_1_out, X);
  not not_2 (not_2_out, Y);
  not not_3 (not_3_out, Z);
  not not_4 (not_4_out, W);
  and and_1 (and_1_out, not_3_out, not_4_out);
  and and_2 (and_2_out, not_1_out, Z, W);
  and and_3 (and_3_out, X, not_3_out);
  and and_4 (and_4_out, X, not_4_out);
  or or_1 (b, not_2_out, and_1_out, and_2_out, and_3_out, and_4_out);
endmodule

module SG_C (
  input  X,
  input  Y,
  input  Z,
  input  W,
  output c
);

  wire and_1_out, and_2_out, and_3_out, not_1_out, not_2_out, not_3_out;

  not not_1 (not_1_out, X);
  not not_2 (not_2_out, Y);
  not not_3 (not_3_out, Z);
  and and_1 (and_1_out, not_1_out, not_3_out);
  and and_2 (and_2_out, Y, Z);
  and and_3 (and_3_out, X, not_2_out);
  or or_1 (c, and_1_out, W, and_2_out, and_3_out);
endmodule

module SG_D (
  input  X,
  input  Y,
  input  Z,
  input  W,
  output d
);

  wire and_1_out, and_2_out, and_3_out, and_4_out, and_5_out, and_6_out, not_1_out, not_2_out, not_3_out,
       not_4_out;

  not not_1 (not_1_out, X);
  not not_2 (not_2_out, Y);
  not not_3 (not_3_out, Z);
  not not_4 (not_4_out, W);
  and and_1 (and_1_out, not_2_out, not_4_out);
  and and_2 (and_2_out, not_1_out, not_2_out, Z);
  and and_3 (and_3_out, not_1_out, Z, not_4_out);
  and and_4 (and_4_out, Y, not_3_out, W);
  and and_5 (and_5_out, X, not_3_out);
  and and_6 (and_6_out, X, Y, W);
  or or_1 (d, and_1_out, and_2_out, and_3_out, and_4_out, and_5_out, and_6_out);
endmodule

module SG_E (
  input  X,
  input  Y,
  input  Z,
  input  W,
  output e
);

  wire and_1_out, and_2_out, and_3_out, not_1_out, not_2_out, not_3_out, not_4_out;

  not not_1 (not_1_out, X);
  not not_2 (not_2_out, Y);
  not not_3 (not_3_out, Z);
  not not_4 (not_4_out, W);
  and and_1 (and_1_out, not_2_out, not_4_out);
  and and_2 (and_2_out, not_1_out, Z, not_4_out);
  and and_3 (and_3_out, X, not_3_out, not_4_out);
  or or_1 (e, and_1_out, and_2_out, and_3_out);
endmodule

module SG_F (
  input  X,
  input  Y,
  input  Z,
  input  W,
  output f
);

  wire and_1_out, and_2_out, and_3_out, and_4_out, and_5_out, and_6_out, not_1_out, not_2_out, not_3_out,
       not_4_out, not_5_out, not_6_out, not_7_out, not_8_out, not_9_out, not_10_out, not_11_out;

  not not_1 (not_1_out, X);
  not not_2 (not_2_out, Z);
  and and_1 (and_1_out, not_1_out, not_2_out, not_3_out);
  not not_3 (not_3_out, W);
  not not_4 (not_4_out, X);
  and and_2 (and_2_out, not_4_out, Y, not_5_out);
  not not_5 (not_5_out, Z);
  not not_6 (not_6_out, X);
  and and_3 (and_3_out, not_6_out, Y, not_7_out);
  not not_7 (not_7_out, W);
  not not_8 (not_8_out, Y);
  and and_4 (and_4_out, X, not_8_out, not_9_out);
  not not_9 (not_9_out, Z);
  not not_10 (not_10_out, Y);
  and and_5 (and_5_out, X, not_10_out, not_11_out);
  not not_11 (not_11_out, W);
  and and_6 (and_6_out, X, Y, Z);
  or or_1 (f, and_1_out, and_2_out, and_3_out, and_4_out, and_5_out, and_6_out);
endmodule

module SG_G (
  input  X,
  input  Y,
  input  Z,
  input  W,
  output g
);

  wire and_1_out, and_2_out, and_3_out, and_4_out, and_5_out, not_1_out, not_2_out, not_3_out, not_4_out;

  not not_1 (not_1_out, X);
  not not_2 (not_2_out, Y);
  not not_3 (not_3_out, Z);
  not not_4 (not_4_out, W);
  and and_1 (and_1_out, not_1_out, not_2_out, Z);
  and and_2 (and_2_out, Y, not_3_out);
  and and_3 (and_3_out, Y, not_4_out);
  and and_4 (and_4_out, X, not_3_out);
  and and_5 (and_5_out, X, Y);
  or or_1 (g, and_1_out, and_2_out, and_3_out, and_4_out, and_5_out);
endmodule

module SG_DP (
  input  X,
  input  Y,
  input  Z,
  input  W,
  output dp
);

  wire and_1_out, and_2_out;

  and and_1 (and_1_out, X, Z);
  and and_2 (and_2_out, X, Y);
  or or_1 (dp, and_1_out, and_2_out);
endmodule

module SG_AI (
  input  X,
  input  Y,
  input  Z,
  input  W,
  output a
);

  wire and_1_out, and_2_out, and_3_out, and_4_out, not_1_out, not_2_out, not_3_out, not_4_out;

  not not_1 (not_1_out, X);
  not not_2 (not_2_out, Y);
  not not_3 (not_3_out, Z);
  not not_4 (not_4_out, W);
  and and_1 (and_1_out, not_1_out, not_2_out, not_3_out, W);
  and and_2 (and_2_out, not_1_out, Y, not_3_out, not_4_out);
  and and_3 (and_3_out, X, not_2_out, Z, W);
  and and_4 (and_4_out, X, Y, Z, not_4_out);
  or or_1 (a, and_1_out, and_2_out, and_3_out, and_4_out);
endmodule

module SG_BI (
  input  X,
  input  Y,
  input  Z,
  input  W,
  output b
);

  wire and_1_out, and_2_out, and_3_out, not_1_out, not_2_out, not_3_out;

  not not_1 (not_1_out, X);
  not not_2 (not_2_out, Z);
  not not_3 (not_3_out, W);
  and and_1 (and_1_out, not_1_out, Y, not_2_out, W);
  and and_2 (and_2_out, not_1_out, Y, Z, not_3_out);
  and and_3 (and_3_out, X, Y, Z, W);
  or or_1 (b, and_1_out, and_2_out, and_3_out);
endmodule

module SG_CI (
  input  X,
  input  Y,
  input  Z,
  input  W,
  output c
);

  wire and_1_out, and_2_out, not_1_out, not_2_out, not_3_out, not_4_out;

  not not_1 (not_1_out, X);
  not not_2 (not_2_out, Y);
  not not_3 (not_3_out, Z);
  not not_4 (not_4_out, W);
  and and_1 (and_1_out, not_1_out, not_2_out, Z, not_4_out);
  and and_2 (and_2_out, X, Y, not_3_out, not_4_out);
  or or_1 (c, and_1_out, and_2_out);
endmodule

module SG_DI (
  input  X,
  input  Y,
  input  Z,
  input  W,
  output d
);

  wire and_1_out, and_2_out, and_3_out, and_4_out, and_5_out, not_1_out, not_2_out, not_3_out, not_4_out;

  not not_1 (not_1_out, X);
  not not_2 (not_2_out, Y);
  not not_3 (not_3_out, Z);
  not not_4 (not_4_out, W);
  and and_1 (and_1_out, not_1_out, not_2_out, not_3_out, W);
  and and_2 (and_2_out, not_1_out, Y, not_3_out, not_4_out);
  and and_3 (and_3_out, not_1_out, Y, Z, W);
  and and_4 (and_4_out, X, not_2_out, Z, W);
  and and_5 (and_5_out, X, Y, Z, not_4_out);
  or or_1 (d, and_1_out, and_2_out, and_3_out, and_4_out, and_5_out);
endmodule

module SG_EI (
  input  X,
  input  Y,
  input  Z,
  input  W,
  output e
);

  wire and_1_out, and_2_out, not_1_out, not_2_out;

  not not_1 (not_1_out, X);
  not not_2 (not_2_out, Z);
  and and_1 (and_1_out, not_1_out, Y, not_2_out);
  and and_2 (and_2_out, X, Y, Z);
  or or_1 (e, W, and_1_out, and_2_out);
endmodule

module SG_FI (
  input  X,
  input  Y,
  input  Z,
  input  W,
  output f
);

  wire and_1_out, and_2_out, and_3_out, and_4_out, and_5_out, not_1_out, not_2_out, not_3_out;

  not not_1 (not_1_out, X);
  not not_2 (not_2_out, Y);
  not not_3 (not_3_out, Z);
  and and_1 (and_1_out, not_1_out, not_2_out, W);
  and and_2 (and_2_out, not_1_out, not_2_out, Z);
  and and_3 (and_3_out, not_1_out, Z, W);
  and and_4 (and_4_out, not_2_out, Z, W);
  and and_5 (and_5_out, X, Y, not_3_out);
  or or_1 (f, and_1_out, and_2_out, and_3_out, and_4_out, and_5_out);
endmodule

module SG_GI (
  input  X,
  input  Y,
  input  Z,
  input  W,
  output g
);

  wire and_1_out, and_2_out, and_3_out, not_1_out, not_2_out, not_3_out;

  not not_1 (not_1_out, X);
  not not_2 (not_2_out, Y);
  not not_3 (not_3_out, Z);
  and and_1 (and_1_out, not_1_out, not_2_out, not_3_out);
  and and_2 (and_2_out, not_1_out, Y, Z, W);
  and and_3 (and_3_out, X, not_2_out, Z);
  or or_1 (g, and_1_out, and_2_out, and_3_out);
endmodule

module SG_DPI (
  input  X,
  input  Y,
  input  Z,
  input  W,
  output dp
);

  wire and_1_out, not_1_out, not_2_out, not_3_out;

  not not_1 (not_1_out, X);
  not not_2 (not_2_out, Y);
  not not_3 (not_3_out, Z);
  and and_1 (and_1_out, not_2_out, not_3_out);
  or or_1 (dp, not_1_out, and_1_out);
endmodule

module descodificador (
  input  X,
  input  in_2
);

  wire undriven;

  SG_A sg_a_1 (.X(X), .Y(in_2));  // open: Z, W, a
  SG_B sg_b_1 (.X(X), .Y(in_2));  // open: Z, W, b
  SG_C sg_c_1 (.X(X), .Y(in_2));  // open: Z, W, c
  SG_D sg_d_1 (.X(X), .Y(in_2));  // open: Z, W, d
  SG_E sg_e_1 (.X(X), .Y(in_2));  // open: Z, W, e
  SG_F sg_f_1 (.X(X), .Y(in_2));  // open: Z, W, f
  SG_G sg_g_1 (.X(X), .Y(in_2));  // open: Z, W, g
  SG_DP sg_dp_1 (.X(X), .Y(in_2));  // open: Z, W, dp
  _7_Segment_Display u_7_segment_display_1 (.g(undriven));  // open: f, a, b, e, d, c, dp
endmodule
