// Logisim project cpu8bitwFSM.circ as structural Verilog: 12 circuits, main circuit cpu8bit
module cpu8bit (
  input  [15:0] ROMData,
  input  clk,
  input  clr,
  input  [7:0] RAMoutdata,
  input  in_5,
  input  in_6,
  input  in_7,
  input  in_8,
  input  in_9,
  input  in_10,
  input  in_11,
  input  in_12,
  output [7:0] ROMAddress,
  output [7:0] RAMaddress,
  output [2:0] StateS,
  output MemRe,
  output MemWe,
  output [7:0] RAMindata,
  output out_19,
  output out_20,
  output out_21,
  output out_22,
  output out_23,
  output out_24,
  output out_25,
  output R30,
  output out_27,
  output out_28,
  output out_29,
  output out_30,
  output out_31,
  output out_32,
  output out_33,
  output R20
);

  wire AluCarry, AluOverf, AluSign, AluZero, AW, IRLoad, Neg, PCInc, PCLoad, SelRegFunc, Zero;
  wire [1:0] ALUCtrl, DSel;
  wire [3:0] multiplexer_2_out, OPCode, RegWAddr;
  wire [7:0] alu_1_r, multiplexer_1_out, registers_1_bbus;

  PC pc_1 (
    .Address({RAMaddress[3:0], RAMaddress[7:4]}), .Address_2(ROMAddress), .select(PCInc), .load(PCLoad),
    .Clock(clk), .Clr(clr));
  // Probe on StateS
  Register #(.width(16)) IR (.D(ROMData), .en(IRLoad), .clk(clk), .Q({OPCode, RegWAddr, RAMaddress}), .clr(clr));
  decoder decoder_1 (
    .IR(OPCode), .Clock(clk), .Clr(clr), .Zero(Zero), .Negative(Neg), .Aluctrl(ALUCtrl), .RAMWrite(MemWe),
    .PCInc(PCInc), .PCload(PCLoad), .RAMRead(MemRe), .Dsel(DSel), .Aw(AW), .ALUZero(AluZero),
    .ALUCarry(AluCarry), .ALUOverf(AluOverf), .ALUSign(AluSign), .IRload(IRLoad), .State(StateS),
    .SelRegFunc(SelRegFunc));
  // Probe on OPCode
  // Probe on {OPCode, RegWAddr, RAMaddress}
  // Probe on DSel
  Multiplexer #(.select(2), .width(8), .enable("false")) multiplexer_1 (
    .in0(RAMaddress), .in1(RAMoutdata), .in2(alu_1_r),
    .in3({in_5, in_6, in_7, in_8, in_9, in_10, in_11, in_12}), .out(multiplexer_1_out), .sel(DSel));
  Multiplexer #(.width(4), .enable("false")) multiplexer_2 (
    .in0(RAMaddress[7:4]), .in1(RegWAddr), .out(multiplexer_2_out), .sel(SelRegFunc));
  // Probe on multiplexer_1_out
  registers registers_1 (
    .Data(multiplexer_1_out), .Awrite(AW), .Abus(RAMindata), .Bbus(registers_1_bbus), .Zero(Zero), .Neg(Neg),
    .Areadreg(multiplexer_2_out), .Breadreg(RAMaddress[3:0]), .Clock(clk), .Clear(clr),
    .R2({out_27, out_28, out_29, out_30, out_31, out_32, out_33, R20}),
    .R3({out_19, out_20, out_21, out_22, out_23, out_24, out_25, R30}), .Wwritereg(RegWAddr));
  alu alu_1 (
    .A(RAMindata), .B(registers_1_bbus), .R(alu_1_r), .Ctrl(ALUCtrl), .Zero(AluZero), .Sign(AluSign),
    .Overf(AluOverf), .Carry(AluCarry));

  // Other names for the same wires on the sheet: RegRBAddr[3:0] = RAMaddress[3:0]; RegRAAddr[3:0] = RAMaddress[7:4];
  //   RamRead = MemRe; RamWrite = MemWe

  // Notes on the sheet:
  //   immediate
  //   ram
  //   alu
  //   P1
endmodule

module alu (
  input  [1:0] Ctrl,
  input  [7:0] A,
  input  [7:0] B,
  output [7:0] R,
  output Zero,
  output Sign,
  output Overf,
  output Carry
);

  wire or_1_out;
  wire [7:0] l_8_bit_adder_3fd74fa9_1_r, l_8_bit_and_2b801d9d_1_r, l_8_bit_or_b7e5c385_1_r, multiplexer_1_out;

  L_8_bit_AND_2b801d9d l_8_bit_and_2b801d9d_1 (.A(A), .B(B), .R(l_8_bit_and_2b801d9d_1_r));
  L_8_bit_OR_b7e5c385 l_8_bit_or_b7e5c385_1 (.A(A), .B(B), .R(l_8_bit_or_b7e5c385_1_r));
  L_8_bit_adder_3fd74fa9 l_8_bit_adder_3fd74fa9_1 (
    .A(A), .B(B), .R(l_8_bit_adder_3fd74fa9_1_r), .Cout(Carry), .Oflw(Overf), .Ctrl(Ctrl[0]));
  Multiplexer #(.width(8), .enable("false")) multiplexer_1 (
    .in0(l_8_bit_and_2b801d9d_1_r), .in1(l_8_bit_or_b7e5c385_1_r), .out(multiplexer_1_out), .sel(Ctrl[0]));
  Multiplexer #(.width(8), .enable("false")) multiplexer_2 (
    .in0(multiplexer_1_out), .in1(l_8_bit_adder_3fd74fa9_1_r), .out(R), .sel(Ctrl[1]));
  not not_1 (Zero, or_1_out);
  or or_1 (or_1_out, R[0], R[1], R[2], R[3], R[4], R[5], R[6], R[7]);

  assign Sign = R[7];
endmodule

module L_1_bit_adder_12ad6c15 (
  input  Cin,
  input  A,
  input  B,
  output Result,
  output Cout
);

  wire and_1_out, and_2_out, xor_1_out;

  and and_1 (and_1_out, B, A);
  xor xor_1 (xor_1_out, A, B);
  and and_2 (and_2_out, xor_1_out, Cin);
  or or_1 (Cout, and_1_out, and_2_out);
  xor xor_2 (Result, Cin, xor_1_out);
endmodule

module L_8_bit_adder_3fd74fa9 (
  input  [7:0] A,
  input  Ctrl,
  input  [7:0] B,
  output [7:0] R,
  output Cout,
  output Oflw
);

  wire and_1_out, and_2_out, l_1_bit_adder_12ad6c15_1_cout, l_1_bit_adder_12ad6c15_2_cout,
       l_1_bit_adder_12ad6c15_3_cout, l_1_bit_adder_12ad6c15_4_cout, l_1_bit_adder_12ad6c15_5_cout,
       l_1_bit_adder_12ad6c15_6_cout, l_1_bit_adder_12ad6c15_7_cout, not_1_out, not_2_out, not_3_out,
       xor_1_out, xor_2_out, xor_3_out, xor_4_out, xor_5_out, xor_6_out, xor_7_out, xor_8_out;

  L_1_bit_adder_12ad6c15 l_1_bit_adder_12ad6c15_1 (
    .A(A[0]), .B(xor_1_out), .Result(R[0]), .Cin(Ctrl), .Cout(l_1_bit_adder_12ad6c15_1_cout));
  xor xor_1 (xor_1_out, Ctrl, B[0]);
  L_1_bit_adder_12ad6c15 l_1_bit_adder_12ad6c15_2 (
    .A(A[1]), .B(xor_2_out), .Result(R[1]), .Cin(l_1_bit_adder_12ad6c15_1_cout),
    .Cout(l_1_bit_adder_12ad6c15_2_cout));
  xor xor_2 (xor_2_out, Ctrl, B[1]);
  L_1_bit_adder_12ad6c15 l_1_bit_adder_12ad6c15_3 (
    .A(A[2]), .B(xor_3_out), .Result(R[2]), .Cin(l_1_bit_adder_12ad6c15_2_cout),
    .Cout(l_1_bit_adder_12ad6c15_3_cout));
  xor xor_3 (xor_3_out, Ctrl, B[2]);
  L_1_bit_adder_12ad6c15 l_1_bit_adder_12ad6c15_4 (
    .A(A[3]), .B(xor_4_out), .Result(R[3]), .Cin(l_1_bit_adder_12ad6c15_3_cout),
    .Cout(l_1_bit_adder_12ad6c15_4_cout));
  xor xor_4 (xor_4_out, Ctrl, B[3]);
  L_1_bit_adder_12ad6c15 l_1_bit_adder_12ad6c15_5 (
    .A(A[4]), .B(xor_5_out), .Result(R[4]), .Cin(l_1_bit_adder_12ad6c15_4_cout),
    .Cout(l_1_bit_adder_12ad6c15_5_cout));
  xor xor_5 (xor_5_out, Ctrl, B[4]);
  L_1_bit_adder_12ad6c15 l_1_bit_adder_12ad6c15_6 (
    .A(A[5]), .B(xor_6_out), .Result(R[5]), .Cin(l_1_bit_adder_12ad6c15_5_cout),
    .Cout(l_1_bit_adder_12ad6c15_6_cout));
  xor xor_6 (xor_6_out, Ctrl, B[5]);
  L_1_bit_adder_12ad6c15 l_1_bit_adder_12ad6c15_7 (
    .A(A[6]), .B(xor_7_out), .Result(R[6]), .Cin(l_1_bit_adder_12ad6c15_6_cout),
    .Cout(l_1_bit_adder_12ad6c15_7_cout));
  xor xor_7 (xor_7_out, Ctrl, B[6]);
  L_1_bit_adder_12ad6c15 l_1_bit_adder_12ad6c15_8 (
    .A(A[7]), .B(xor_8_out), .Result(R[7]), .Cin(l_1_bit_adder_12ad6c15_7_cout), .Cout(Cout));
  xor xor_8 (xor_8_out, Ctrl, B[7]);
  not not_1 (not_1_out, R[7]);
  not not_2 (not_2_out, xor_8_out);
  not not_3 (not_3_out, A[7]);
  and and_1 (and_1_out, not_1_out, xor_8_out, A[7]);
  and and_2 (and_2_out, R[7], not_2_out, not_3_out);
  or or_1 (Oflw, and_1_out, and_2_out);
endmodule

module L_8_bit_AND_2b801d9d (
  input  [7:0] A,
  input  [7:0] B,
  output [7:0] R
);

  and and_1 (R[0], A[0], B[0]);
  and and_2 (R[1], A[1], B[1]);
  and and_3 (R[2], A[2], B[2]);
  and and_4 (R[3], A[3], B[3]);
  and and_5 (R[4], A[4], B[4]);
  and and_6 (R[5], A[5], B[5]);
  and and_7 (R[6], A[6], B[6]);
  and and_8 (R[7], A[7], B[7]);
endmodule

module L_8_bit_OR_b7e5c385 (
  input  [7:0] A,
  input  [7:0] B,
  output [7:0] R
);

  or or_1 (R[0], A[0], B[0]);
  or or_2 (R[1], A[1], B[1]);
  or or_3 (R[2], A[2], B[2]);
  or or_4 (R[3], A[3], B[3]);
  or or_5 (R[4], A[4], B[4]);
  or or_6 (R[5], A[5], B[5]);
  or or_7 (R[6], A[6], B[6]);
  or or_8 (R[7], A[7], B[7]);
endmodule

// Wreg
module registers (
  input  [3:0] Areadreg,
  input  [3:0] Wwritereg,
  input  [3:0] Breadreg,
  input  [7:0] Data,
  input  Awrite,
  input  Clock,
  input  Clear,
  output [7:0] Abus,
  output [7:0] Bbus,
  output Zero,
  output Neg,
  output [7:0] R2,
  output [7:0] R3
);

  wire demultiplexer_1_out0, demultiplexer_1_out1, demultiplexer_1_out2, demultiplexer_1_out3, or_1_out;
  wire [7:0] register_1_q, register_2_q;

  Demultiplexer #(.select(2), .enable("false")) demultiplexer_1 (
    .out0(demultiplexer_1_out0), .out1(demultiplexer_1_out1), .out2(demultiplexer_1_out2),
    .out3(demultiplexer_1_out3), .in(Awrite), .sel(Wwritereg[1:0]));
  Register register_1 (.D(Data), .en(demultiplexer_1_out0), .clk(Clock), .Q(register_1_q), .clr(Clear));
  Register register_2 (.D(Data), .en(demultiplexer_1_out1), .clk(Clock), .Q(register_2_q), .clr(Clear));
  Register register_3 (.D(Data), .en(demultiplexer_1_out2), .clk(Clock), .Q(R2), .clr(Clear));
  Register register_4 (.D(Data), .en(demultiplexer_1_out3), .clk(Clock), .Q(R3), .clr(Clear));
  // Probe on register_1_q
  // Probe on register_2_q
  // Probe on R2
  // Probe on R3
  Multiplexer #(.select(2), .width(8), .enable("false")) multiplexer_1 (
    .in0(register_1_q), .in1(register_2_q), .in2(R2), .in3(R3), .out(Abus), .sel(Areadreg[1:0]));
  Multiplexer #(.select(2), .width(8), .enable("false")) multiplexer_2 (
    .in0(register_1_q), .in1(register_2_q), .in2(R2), .in3(R3), .out(Bbus), .sel(Breadreg[1:0]));
  or or_1 (or_1_out, Abus[0], Abus[1], Abus[2], Abus[3], Abus[4], Abus[5], Abus[6], Abus[7]);
  not not_1 (Zero, or_1_out);

  assign Neg = Abus[7];
endmodule

module PC (
  input  select,
  input  [7:0] Address,
  input  load,
  input  Clock,
  input  Clr,
  output [7:0] Address_2
);

  wire [7:0] l_8_bit_adder_3fd74fa9_1_r, multiplexer_1_out;

  Multiplexer #(.width(8), .enable("false")) multiplexer_1 (
    .in0(Address), .in1(l_8_bit_adder_3fd74fa9_1_r), .out(multiplexer_1_out), .sel(select));
  Register register_1 (.D(multiplexer_1_out), .en(load), .clk(Clock), .Q(Address_2), .clr(Clr));
  L_8_bit_adder_3fd74fa9 l_8_bit_adder_3fd74fa9_1 (
    .A(Address_2), .B(8'h1), .R(l_8_bit_adder_3fd74fa9_1_r), .Ctrl(1'b0));  // open: Cout, Oflw
endmodule

// Reg
module decoder (
  input  ALUZero,
  input  ALUCarry,
  input  ALUOverf,
  input  ALUSign,
  input  Zero,
  input  Negative,
  input  [3:0] IR,
  input  Clock,
  input  Clr,
  output IRload,
  output SelRegFunc,
  output [1:0] Dsel,
  output [1:0] Aluctrl,
  output RAMWrite,
  output RAMRead,
  output PCload,
  output Aw,
  output PCInc,
  output [2:0] State
);

  wire and_1_out, and_2_out, and_3_out, and_4_out, InstrEnable, jmpe, jmpline, jmpne, jmpnz, jmpz, jpmline;
  wire [2:0] NstateSignal;

  Register #(.width(3)) register_1 (.D(NstateSignal), .en(1'b1), .clk(Clock), .Q(State), .clr(Clr));
  Multiplexer #(.select(4), .width(13)) multiplexer_1 (
    .in0(13'h23), .in1(13'ha4), .in2(13'h51), .in3(13'h1), .in4(13'h71), .in5(13'h69), .in6(13'h41),
    .in7(13'h61), .in8(13'h180), .in9(13'h280), .in10(13'h480), .in11(13'h880), .in12(13'h1080),
    .in13({13{1'b0}}), .in14({13{1'b0}}), .in15({13{1'b0}}),
    .out({jmpne, jmpe, jmpnz, jmpz, jmpline, SelRegFunc, Dsel, Aluctrl, RAMWrite, RAMRead, Aw}), .sel(IR),
    .en(InstrEnable));
  and and_1 (and_1_out, jmpz, Zero);
  and and_2 (and_2_out, jmpnz, ~Zero);  // AND_Gate
  and and_3 (and_3_out, jmpe, Negative);
  and and_4 (and_4_out, jmpne, ~Negative);  // AND_Gate
  or or_1 (jpmline, jmpline, and_1_out, and_2_out, and_3_out, and_4_out);
  and and_5 (InstrEnable, State[1], State[0]);
  and and_6 (IRload, ~State[1], State[0]);  // AND_Gate
  or or_2 (PCload, IRload, State[2]);
  not not_1 (PCInc, State[2]);
  FSMDec fsmdec_1 (
    .jmp(jpmline), .State2(State[2]), .State1(State[1]), .State0(State[0]), .Nstate2(NstateSignal[2]),
    .Nstate1(NstateSignal[1]), .Nstate0(NstateSignal[0]));

  // Other names for the same wires on the sheet: Neg = Negative; StateSignal[2:0] = State

  // Notes on the sheet:
  //   jeq
  //   jmp
  //   jne
  //   jgt
  //   jlt
  //   Add
  //   LI
  //   Sub
  //   LW
  //   SW
endmodule

module main (
  input  [7:0] in_1,
  output [7:0] out_2,
  output [7:0] out_3
);

  wire button_1_out, clock_1_out, uP_memre, uP_memwe;
  wire [2:0] uP_states;
  wire [7:0] ram_1_dout, uP_ramaddress, uP_ramindata, uP_romaddress;
  wire [15:0] rom_1_data;

  Clock sysclk ();  // open: out
  ROM #(.dataWidth(16)) rom_1 (.addr(uP_romaddress), .data(rom_1_data));
  // Probe on uP_romaddress
  // Probe on rom_1_data
  cpu8bit uP (
    .clk(clock_1_out), .clr(button_1_out), .out_19(out_2[7]), .out_20(out_2[6]), .out_21(out_2[5]),
    .out_22(out_2[4]), .out_23(out_2[3]), .out_24(out_2[2]), .out_25(out_2[1]), .R30(out_2[0]),
    .in_5(in_1[7]), .in_6(in_1[6]), .in_7(in_1[5]), .in_8(in_1[4]), .in_9(in_1[3]), .in_10(in_1[2]),
    .in_11(in_1[1]), .in_12(in_1[0]), .out_27(out_3[7]), .out_28(out_3[6]), .out_29(out_3[5]),
    .out_30(out_3[4]), .out_31(out_3[3]), .out_32(out_3[2]), .out_33(out_3[1]), .R20(out_3[0]),
    .RAMindata(uP_ramindata), .RAMaddress(uP_ramaddress), .RAMoutdata(ram_1_dout),
    .ROMAddress(uP_romaddress), .ROMData(rom_1_data), .MemRe(uP_memre), .MemWe(uP_memwe), .StateS(uP_states));
  Clock clock_1 (.out(clock_1_out));
  Button button_1 (.out(button_1_out));
  // Probe on uP_ramaddress
  // Probe on uP_ramindata
  RAM #(.databus("bibus")) ram_1 (
    .addr(uP_ramaddress), .we(uP_memwe), .oe(uP_memre), .clk(clock_1_out), .din(uP_ramindata),
    .dout(ram_1_dout));
  // Probe on uP_states
  // Probe on ram_1_dout

  // Notes on the sheet:
  //   contents of rom_1 (hex, n*v repeats v):
  //   3320 3205 1200 1301 0 101 2010 920a 1203 1204 1205 1206 8000
endmodule

module FSMDec (
  input  jmp,
  input  State2,
  input  State1,
  input  State0,
  output Nstate2,
  output Nstate1,
  output Nstate0
);

  wire and_1_out, and_2_out, and_3_out, and_4_out, and_5_out, not_1_out, not_2_out, not_3_out, not_4_out,
       not_5_out, not_6_out, not_7_out, not_8_out, not_9_out, not_10_out, not_11_out;

  not not_1 (not_1_out, State2);
  not not_2 (not_2_out, State2);
  and and_1 (and_1_out, not_2_out, not_3_out, State0);
  not not_3 (not_3_out, State1);
  not not_4 (not_4_out, State2);
  and and_2 (and_2_out, not_4_out, State1, not_5_out);
  not not_5 (not_5_out, State0);
  not not_6 (not_6_out, State2);
  and and_3 (and_3_out, not_6_out, not_7_out);
  not not_7 (not_7_out, State0);
  not not_8 (not_8_out, State1);
  and and_4 (and_4_out, not_8_out, not_9_out);
  not not_9 (not_9_out, State0);
  not not_10 (not_10_out, jmp);
  and and_5 (and_5_out, not_10_out, not_11_out, State1);
  not not_11 (not_11_out, State2);
  and and_6 (Nstate2, jmp, not_1_out, State1, State0);
  or or_1 (Nstate1, and_1_out, and_2_out);
  or or_2 (Nstate0, and_3_out, and_4_out, and_5_out);
endmodule

module JumpDec (
  input  ZeroS,
  input  NegS,
  input  State2,
  output Jump
);

  wire and_1_out, not_1_out;

  not not_1 (not_1_out, State2);
  and and_1 (and_1_out, ZeroS, NegS);
  or or_1 (Jump, not_1_out, and_1_out);
endmodule
