// Logisim project testepratico1.circ as structural Verilog
module pergunta1 (
  input  A3,
  input  A2,
  input  A1,
  input  A0,
  output G3,
  output G2,
  output G1,
  output G0
);

  wire and_1_out, and_2_out, and_3_out, and_4_out, and_5_out, and_6_out, not_1_out, not_2_out, not_3_out,
       not_4_out;

  not not_1 (not_1_out, A3);
  not not_2 (not_2_out, A2);
  not not_3 (not_3_out, A1);
  not not_4 (not_4_out, A0);
  and and_1 (and_1_out, not_1_out, A2);
  and and_2 (and_2_out, A3, not_2_out);
  and and_3 (and_3_out, not_2_out, A1);
  and and_4 (and_4_out, A2, not_3_out);
  and and_5 (and_5_out, not_3_out, A0);
  and and_6 (and_6_out, A1, not_4_out);
  or or_1 (G2, and_1_out, and_2_out);
  or or_2 (G1, and_3_out, and_4_out);
  or or_3 (G0, and_5_out, and_6_out);

  assign G3 = A3;
endmodule

module somador_completo_p2 (
  input  A,
  input  B,
  input  Cin,
  output S,
  output Cout
);

  wire and_1_out, and_2_out, and_3_out, and_4_out, and_5_out, and_6_out, and_7_out, not_1_out, not_2_out,
       not_3_out;

  not not_1 (not_1_out, A);
  not not_2 (not_2_out, B);
  not not_3 (not_3_out, Cin);
  and and_1 (and_1_out, not_1_out, not_2_out, Cin);
  and and_2 (and_2_out, not_1_out, B, not_3_out);
  and and_3 (and_3_out, A, not_2_out, not_3_out);
  and and_4 (and_4_out, A, B, Cin);
  and and_5 (and_5_out, B, Cin);
  and and_6 (and_6_out, A, Cin);
  and and_7 (and_7_out, A, B);
  or or_1 (S, and_1_out, and_2_out, and_3_out, and_4_out);
  or or_2 (Cout, and_5_out, and_6_out, and_7_out);
endmodule

module pergunta2 (
  input  in_1,
  input  in_2,
  input  in_3,
  input  in_4,
  input  in_5,
  input  in_6,
  input  in_7,
  input  in_8,
  input  in_9,
  output out_10,
  output out_11,
  output out_12,
  output out_13,
  output out_14
);

  wire somador_completo_p2_1_cout, somador_completo_p2_2_cout, somador_completo_p2_3_cout;

  somador_completo_p2 somador_completo_p2_1 (
    .A(in_1), .B(in_2), .Cin(in_3), .S(out_10), .Cout(somador_completo_p2_1_cout));
  somador_completo_p2 somador_completo_p2_2 (
    .A(in_4), .B(in_5), .Cin(somador_completo_p2_1_cout), .S(out_11), .Cout(somador_completo_p2_2_cout));
  somador_completo_p2 somador_completo_p2_3 (
    .A(in_6), .B(in_7), .Cin(somador_completo_p2_2_cout), .S(out_12), .Cout(somador_completo_p2_3_cout));
  somador_completo_p2 somador_completo_p2_4 (
    .A(in_8), .B(in_9), .Cin(somador_completo_p2_3_cout), .S(out_13), .Cout(out_14));

  // Notes on the sheet:
  //   Implemente em Logisim um somador de 4 bits usando uma cascata de somadores Full Adder de um bit.
endmodule
