// Logisim project trabalho6_SofiaeRuben.circ as structural Verilog: 2 circuits, main circuit main
module main (
  input  in_1,
  input  in_2,
  input  in_3,
  input  in_4,
  input  in_5,
  input  in_6,
  input  in_7
);

  wire c74ls163_1_q0, c74ls163_1_q1, c74ls163_1_q2, c74ls163_1_q3, clock_1_out, nand_1_out, seg7_1_a,
       seg7_1_b, seg7_1_c, seg7_1_d, seg7_1_e, seg7_1_f, seg7_1_g;

  Clock clock_1 (.out(clock_1_out));
  C74ls163 c74ls163_1 (
    .ENP(in_1), .ENT(in_2), .LOAD_N(nand_1_out), .CLEAR_N(in_3), .CLK(clock_1_out), .A(in_4), .B(in_5),
    .C(in_6), .D(in_7), .Q0(c74ls163_1_q0), .Q1(c74ls163_1_q1), .Q2(c74ls163_1_q2), .Q3(c74ls163_1_q3));  // open: CO
  nand nand_1 (nand_1_out, c74ls163_1_q0, ~c74ls163_1_q1, ~c74ls163_1_q2, c74ls163_1_q3);  // NAND_Gate
  seg7 seg7_1 (
    .x(c74ls163_1_q3), .y(c74ls163_1_q2), .z(c74ls163_1_q1), .w(c74ls163_1_q0), .a(seg7_1_a), .b(seg7_1_b),
    .c(seg7_1_c), .d(seg7_1_d), .e(seg7_1_e), .f(seg7_1_f), .g(seg7_1_g));
  _7_Segment_Display u_7_segment_display_1 (
    .g(seg7_1_g), .f(seg7_1_f), .a(seg7_1_a), .b(seg7_1_b), .e(seg7_1_e), .d(seg7_1_d), .c(seg7_1_c));  // open: dp
endmodule

module seg7 (
  input  x,
  input  y,
  input  z,
  input  w,
  output a,
  output b,
  output c,
  output d,
  output e,
  output f,
  output g
);

  wire and_1_out, and_2_out, and_3_out, and_4_out, and_5_out, and_6_out, and_7_out, and_8_out, and_9_out,
       and_10_out, and_11_out, and_12_out, and_13_out, and_14_out, and_15_out, and_16_out, and_17_out,
       not_1_out, not_2_out, not_3_out;

  not not_1 (not_1_out, y);
  not not_2 (not_2_out, z);
  not not_3 (not_3_out, w);
  and and_1 (and_1_out, not_1_out, not_3_out);
  and and_2 (and_2_out, y, w);
  and and_3 (and_3_out, not_2_out, not_3_out);
  and and_4 (and_4_out, z, w);
  or or_1 (c, not_2_out, w, y);
  and and_5 (and_5_out, not_1_out, not_3_out);
  and and_6 (and_6_out, not_1_out, z);
  and and_7 (and_7_out, z, not_3_out);
  and and_8 (and_8_out, y, not_2_out, w);
  and and_9 (and_9_out, not_1_out, not_3_out);
  and and_10 (and_10_out, z, not_3_out);
  and and_11 (and_11_out, not_2_out, not_3_out);
  and and_12 (and_12_out, y, not_2_out);
  and and_13 (and_13_out, y, not_3_out);
  and and_14 (and_14_out, x, not_2_out);
  and and_15 (and_15_out, not_1_out, z);
  and and_16 (and_16_out, y, not_2_out);
  and and_17 (and_17_out, y, not_3_out);
  or or_2 (a, and_1_out, z, and_2_out, x);
  or or_3 (b, not_1_out, and_3_out, and_4_out);
  or or_4 (d, and_5_out, and_6_out, and_7_out, and_8_out);
  or or_5 (e, and_9_out, and_10_out);
  or or_6 (f, and_11_out, and_12_out, and_13_out, and_14_out);
  or or_7 (g, and_15_out, and_16_out, and_17_out, x);
endmodule
