// Logisim project ficha_3.circ as structural Verilog: 8 circuits, main circuit main
module main (
);

  somador_cascata somador_cascata_1 ();  // open: in_1, in_2, in_3, in_4, in_5, in_6, in_7, in_8, in_9, in_10, in_11, in_12, in_13, in_14, in_15, in_16, in_17, out_18, out_19, out_20, out_21, out_22, out_23, out_24, out_25, out_26
endmodule

module meio_somador (
  input  A,
  input  B,
  output soma,
  output cout
);

  wire and_1_out, and_2_out, not_1_out, not_2_out;

  not not_1 (not_1_out, A);
  not not_2 (not_2_out, B);
  and and_1 (and_1_out, not_1_out, B);
  and and_2 (and_2_out, A, not_2_out);
  and and_3 (cout, A, B);
  or or_1 (soma, and_1_out, and_2_out);
endmodule

module somador_completo (
  input  A,
  input  B,
  input  Cin,
  output Soma,
  output Cout
);

  wire and_1_out, and_2_out, and_3_out, and_4_out, and_5_out, and_6_out, and_7_out, not_1_out, not_2_out,
       not_3_out;

  not not_1 (not_1_out, A);
  not not_2 (not_2_out, B);
  not not_3 (not_3_out, Cin);
  and and_1 (and_1_out, not_1_out, not_2_out, Cin);
  and and_2 (and_2_out, not_1_out, B, not_3_out);
  and and_3 (and_3_out, A, not_2_out, not_3_out);
  and and_4 (and_4_out, A, B, Cin);
  and and_5 (and_5_out, B, Cin);
  and and_6 (and_6_out, A, Cin);
  and and_7 (and_7_out, A, B);
  or or_1 (Soma, and_1_out, and_2_out, and_3_out, and_4_out);
  or or_2 (Cout, and_5_out, and_6_out, and_7_out);
endmodule

module meios_somadores_juntos (
  input  in_1,
  input  in_2,
  input  in_3,
  output out_4,
  output out_5
);

  wire meio_somador_1_cout, meio_somador_1_soma, meio_somador_2_cout;

  meio_somador meio_somador_1 (.A(in_1), .B(in_2), .soma(meio_somador_1_soma), .cout(meio_somador_1_cout));
  meio_somador meio_somador_2 (.A(meio_somador_1_soma), .B(in_3), .soma(out_4), .cout(meio_somador_2_cout));
  or or_1 (out_5, meio_somador_2_cout, meio_somador_1_cout);
endmodule

module somador_cascata (
  input  in_1,
  input  in_2,
  input  in_3,
  input  in_4,
  input  in_5,
  input  in_6,
  input  in_7,
  input  in_8,
  input  in_9,
  input  in_10,
  input  in_11,
  input  in_12,
  input  in_13,
  input  in_14,
  input  in_15,
  input  in_16,
  input  in_17,
  output out_18,
  output out_19,
  output out_20,
  output out_21,
  output out_22,
  output out_23,
  output out_24,
  output out_25,
  output out_26
);

  wire meios_somadores_juntos_1_out_5, meios_somadores_juntos_2_out_5, meios_somadores_juntos_3_out_5,
       meios_somadores_juntos_4_out_5, meios_somadores_juntos_5_out_5, meios_somadores_juntos_6_out_5,
       meios_somadores_juntos_7_out_5;

  meios_somadores_juntos meios_somadores_juntos_1 (
    .in_1(in_1), .in_2(in_2), .in_3(in_3), .out_4(out_18), .out_5(meios_somadores_juntos_1_out_5));
  meios_somadores_juntos meios_somadores_juntos_2 (
    .in_1(in_10), .in_2(in_11), .in_3(meios_somadores_juntos_7_out_5), .out_4(out_22),
    .out_5(meios_somadores_juntos_2_out_5));
  meios_somadores_juntos meios_somadores_juntos_3 (
    .in_1(in_4), .in_2(in_5), .in_3(meios_somadores_juntos_1_out_5), .out_4(out_19),
    .out_5(meios_somadores_juntos_3_out_5));
  meios_somadores_juntos meios_somadores_juntos_4 (
    .in_1(in_12), .in_2(in_13), .in_3(meios_somadores_juntos_2_out_5), .out_4(out_23),
    .out_5(meios_somadores_juntos_4_out_5));
  meios_somadores_juntos meios_somadores_juntos_5 (
    .in_1(in_6), .in_2(in_7), .in_3(meios_somadores_juntos_3_out_5), .out_4(out_20),
    .out_5(meios_somadores_juntos_5_out_5));
  meios_somadores_juntos meios_somadores_juntos_6 (
    .in_1(in_14), .in_2(in_15), .in_3(meios_somadores_juntos_4_out_5), .out_4(out_24),
    .out_5(meios_somadores_juntos_6_out_5));
  meios_somadores_juntos meios_somadores_juntos_7 (
    .in_1(in_8), .in_2(in_9), .in_3(meios_somadores_juntos_5_out_5), .out_4(out_21),
    .out_5(meios_somadores_juntos_7_out_5));
  meios_somadores_juntos meios_somadores_juntos_8 (
    .in_1(in_16), .in_2(in_17), .in_3(meios_somadores_juntos_6_out_5), .out_4(out_25), .out_5(out_26));
endmodule

module comparadores (
  input  A,
  input  B,
  output Q1,
  output Q2,
  output Q3
);

  wire and_1_out, and_2_out, not_1_out, not_2_out;

  not not_1 (not_1_out, A);
  not not_2 (not_2_out, B);
  and and_1 (and_1_out, not_1_out, not_2_out);
  and and_2 (and_2_out, A, B);
  and and_3 (Q2, A, not_2_out);
  and and_4 (Q3, not_1_out, B);
  or or_1 (Q1, and_1_out, and_2_out);
endmodule

module comparador_8bits (
  input  Q1_anterior,
  input  Q2_anterior,
  input  Q3_anterior,
  input  A,
  input  B,
  output Q1,
  output Q2,
  output Q3
);

  wire and_2_out, and_3_out, comparadores_1_q1, comparadores_1_q2, comparadores_1_q3;

  comparadores comparadores_1 (.A(A), .B(B), .Q1(comparadores_1_q1), .Q2(comparadores_1_q2), .Q3(comparadores_1_q3));
  and and_1 (Q1, Q1_anterior, comparadores_1_q1);
  and and_2 (and_2_out, Q1_anterior, comparadores_1_q2);
  and and_3 (and_3_out, Q1_anterior, comparadores_1_q3);
  or or_1 (Q2, Q2_anterior, and_2_out);
  or or_2 (Q3, and_3_out, Q3_anterior);
endmodule

module comparador_cascata (
  input  in_1,
  input  in_2,
  input  in_3,
  input  in_4,
  input  in_5,
  input  in_6,
  input  in_7,
  input  in_8,
  input  in_9,
  input  in_10,
  input  in_11,
  input  in_12,
  input  in_13,
  input  in_14,
  input  in_15,
  input  in_16,
  input  in_17,
  input  in_18,
  input  in_19,
  output out_20,
  output out_21,
  output out_22
);

  wire comparador_8bits_1_q1, comparador_8bits_1_q2, comparador_8bits_1_q3, comparador_8bits_2_q1,
       comparador_8bits_2_q2, comparador_8bits_2_q3, comparador_8bits_3_q1, comparador_8bits_3_q2,
       comparador_8bits_3_q3, comparador_8bits_4_q1, comparador_8bits_4_q2, comparador_8bits_4_q3,
       comparador_8bits_5_q1, comparador_8bits_5_q2, comparador_8bits_5_q3, comparador_8bits_6_q1,
       comparador_8bits_6_q2, comparador_8bits_6_q3, comparador_8bits_8_q1, comparador_8bits_8_q2,
       comparador_8bits_8_q3;

  comparador_8bits comparador_8bits_1 (
    .Q1_anterior(comparador_8bits_8_q1), .Q2_anterior(comparador_8bits_8_q2),
    .Q3_anterior(comparador_8bits_8_q3), .A(in_12), .B(in_13), .Q1(comparador_8bits_1_q1),
    .Q2(comparador_8bits_1_q2), .Q3(comparador_8bits_1_q3));
  comparador_8bits comparador_8bits_2 (
    .Q1_anterior(in_1), .Q2_anterior(in_2), .Q3_anterior(in_3), .A(in_4), .B(in_5),
    .Q1(comparador_8bits_2_q1), .Q2(comparador_8bits_2_q2), .Q3(comparador_8bits_2_q3));
  comparador_8bits comparador_8bits_3 (
    .Q1_anterior(comparador_8bits_1_q1), .Q2_anterior(comparador_8bits_1_q2),
    .Q3_anterior(comparador_8bits_1_q3), .A(in_14), .B(in_15), .Q1(comparador_8bits_3_q1),
    .Q2(comparador_8bits_3_q2), .Q3(comparador_8bits_3_q3));
  comparador_8bits comparador_8bits_4 (
    .Q1_anterior(comparador_8bits_2_q1), .Q2_anterior(comparador_8bits_2_q2),
    .Q3_anterior(comparador_8bits_2_q3), .A(in_6), .B(in_7), .Q1(comparador_8bits_4_q1),
    .Q2(comparador_8bits_4_q2), .Q3(comparador_8bits_4_q3));
  comparador_8bits comparador_8bits_5 (
    .Q1_anterior(comparador_8bits_3_q1), .Q2_anterior(comparador_8bits_3_q2),
    .Q3_anterior(comparador_8bits_3_q3), .A(in_16), .B(in_17), .Q1(comparador_8bits_5_q1),
    .Q2(comparador_8bits_5_q2), .Q3(comparador_8bits_5_q3));
  comparador_8bits comparador_8bits_6 (
    .Q1_anterior(comparador_8bits_4_q1), .Q2_anterior(comparador_8bits_4_q2),
    .Q3_anterior(comparador_8bits_4_q3), .A(in_8), .B(in_9), .Q1(comparador_8bits_6_q1),
    .Q2(comparador_8bits_6_q2), .Q3(comparador_8bits_6_q3));
  comparador_8bits comparador_8bits_7 (
    .Q1_anterior(comparador_8bits_5_q1), .Q2_anterior(comparador_8bits_5_q2),
    .Q3_anterior(comparador_8bits_5_q3), .A(in_18), .B(in_19), .Q1(out_20), .Q2(out_21), .Q3(out_22));
  comparador_8bits comparador_8bits_8 (
    .Q1_anterior(comparador_8bits_6_q1), .Q2_anterior(comparador_8bits_6_q2),
    .Q3_anterior(comparador_8bits_6_q3), .A(in_10), .B(in_11), .Q1(comparador_8bits_8_q1),
    .Q2(comparador_8bits_8_q2), .Q3(comparador_8bits_8_q3));
endmodule
