// Logisim project trabalho5.circ as structural Verilog
module gerador_sequencia (
  input  s2,
  input  s1,
  input  s0,
  input  a,
  output r,
  output n2,
  output n1,
  output n0
);

  wire and_1_out, and_2_out, and_4_out, and_5_out, and_6_out, and_7_out, not_1_out, not_2_out, not_3_out;

  not not_1 (not_1_out, s2);
  not not_2 (not_2_out, s1);
  not not_3 (not_3_out, s0);
  and and_1 (and_1_out, not_2_out, s0);
  and and_2 (and_2_out, s1, not_3_out);
  and and_3 (n2, s1, s0);
  and and_4 (and_4_out, not_2_out, s0);
  and and_5 (and_5_out, s1, not_3_out);
  and and_6 (and_6_out, not_1_out, not_3_out, a);
  and and_7 (and_7_out, s1, not_3_out);
  or or_1 (r, and_1_out, and_2_out, s2);
  or or_2 (n1, and_4_out, and_5_out);
  or or_3 (n0, and_6_out, and_7_out);
endmodule

module gerador_sequencia_memoria (
  input  in_1,
  output out_2
);

  wire clock_1_out, d_ff_1_q, d_ff_2_q, d_ff_3_q, gerador_sequencia_1_n0, gerador_sequencia_1_n1,
       gerador_sequencia_1_n2;

  Clock clock_1 (.out(clock_1_out));
  D_Flip_Flop d_ff_1 (.D(gerador_sequencia_1_n1), .clk(clock_1_out), .Q(d_ff_1_q));  // open: Qn, preset, reset
  D_Flip_Flop d_ff_2 (.D(gerador_sequencia_1_n0), .clk(clock_1_out), .Q(d_ff_2_q));  // open: Qn, preset, reset
  D_Flip_Flop d_ff_3 (.D(gerador_sequencia_1_n2), .clk(clock_1_out), .Q(d_ff_3_q));  // open: Qn, preset, reset
  gerador_sequencia gerador_sequencia_1 (
    .s2(d_ff_3_q), .s1(d_ff_1_q), .s0(d_ff_2_q), .a(in_1), .r(out_2), .n2(gerador_sequencia_1_n2),
    .n1(gerador_sequencia_1_n1), .n0(gerador_sequencia_1_n0));
endmodule

module detetor_sequencia (
  input  s2,
  input  s1,
  input  s0,
  input  r,
  output n2,
  output n1,
  output n0,
  output certo
);

  wire and_1_out, and_2_out, and_3_out, and_4_out, and_5_out, and_6_out, not_1_out, not_2_out, not_3_out,
       not_4_out;

  not not_1 (not_1_out, s2);
  not not_2 (not_2_out, s1);
  not not_3 (not_3_out, s0);
  not not_4 (not_4_out, r);
  and and_1 (and_1_out, not_1_out, s1, s0, not_4_out);
  and and_2 (and_2_out, s2, not_2_out, r);
  and and_3 (and_3_out, s2, not_3_out, r);
  and and_4 (and_4_out, not_1_out, not_2_out, s0, not_4_out);
  and and_5 (and_5_out, s1, not_3_out, r);
  and and_6 (and_6_out, s2, not_2_out, s0, r);
  and and_7 (n0, not_3_out, r);
  and and_8 (certo, s2, s1, not_3_out, r);
  or or_1 (n2, and_1_out, and_2_out, and_3_out);
  or or_2 (n1, and_4_out, and_5_out, and_6_out);
endmodule

module detetor_sequencia_memoria (
  input  in_1,
  input  [7:0] in_2,
  output out_3
);

  wire clock_1_out, clock_2_out, d_ff_1_q, d_ff_2_q, d_ff_3_q, detetor_sequencia_1_certo,
       detetor_sequencia_1_n0, detetor_sequencia_1_n1, detetor_sequencia_1_n2, shift_esquerda_1_util;

  Clock clock_1 (.out(clock_1_out));
  shift_esquerda shift_esquerda_1 (.shift(in_1), .sequencia(in_2), .clk(clock_1_out), .util(shift_esquerda_1_util));
  detetor_sequencia detetor_sequencia_1 (
    .s2(d_ff_1_q), .s1(d_ff_2_q), .s0(d_ff_3_q), .r(shift_esquerda_1_util), .n2(detetor_sequencia_1_n2),
    .n1(detetor_sequencia_1_n1), .n0(detetor_sequencia_1_n0), .certo(detetor_sequencia_1_certo));
  Clock clock_2 (.out(clock_2_out));
  D_Flip_Flop d_ff_1 (.D(detetor_sequencia_1_n2), .clk(clock_2_out), .Q(d_ff_1_q));  // open: Qn, preset, reset
  D_Flip_Flop d_ff_2 (.D(detetor_sequencia_1_n1), .clk(clock_2_out), .Q(d_ff_2_q));  // open: Qn, preset, reset
  D_Flip_Flop d_ff_3 (.D(detetor_sequencia_1_n0), .clk(clock_2_out), .Q(d_ff_3_q));  // open: Qn, preset, reset
  D_Flip_Flop d_ff_4 (.D(detetor_sequencia_1_certo), .clk(clock_2_out), .Q(out_3));  // open: Qn, preset, reset
endmodule

module shift_esquerda (
  input  shift,
  input  [7:0] sequencia,
  input  clk,
  output util
);

  wire [7:0] multiplexer_1_out;
  wire [7:1] register_1_q;

  // Probe on {util, register_1_q}
  Multiplexer #(.enable("false"), .width(8)) multiplexer_1 (
    .in0(sequencia), .in1({register_1_q, 1'b0}), .out(multiplexer_1_out), .sel(shift));
  Register register_1 (.D(multiplexer_1_out), .en(1'b1), .clk(clk), .Q({util, register_1_q}));  // open: clr
endmodule
