// Logisim project 74ls163A.circ as structural Verilog: 1 circuit, main circuit C74ls163
// ls163
module C74ls163 (
  input  ENP,
  input  ENT,
  input  LOAD_N,
  input  CLEAR_N,
  input  CLK,
  input  A,
  input  B,
  input  C,
  input  D,
  output CO,
  output Q0,
  output Q1,
  output Q2,
  output Q3
);

  wire and_1_out, and_2_out, not_1_out;
  wire [1:0] Sel;
  wire [3:0] adder_1_out, multiplexer_1_out;

  not not_1 (not_1_out, LOAD_N);
  Multiplexer #(.select(2), .width(4), .enable("false")) multiplexer_1 (
    .in0(4'b0000), .in1({D, C, B, A}), .in2({Q3, Q2, Q1, Q0}), .in3(adder_1_out), .out(multiplexer_1_out),
    .sel(Sel));
  and and_1 (and_1_out, CLEAR_N, not_1_out);
  and and_2 (and_2_out, ENP, ENT, CLEAR_N);
  and and_3 (Sel[1], LOAD_N, CLEAR_N);
  Register #(.width(4)) register_1 (.D(multiplexer_1_out), .en(1'b1), .clk(CLK), .Q({Q3, Q2, Q1, Q0}));  // open: clr
  or or_1 (Sel[0], and_1_out, and_2_out);
  Adder #(.width(4)) adder_1 (.a({Q3, Q2, Q1, Q0}), .b(4'b0001), .out(adder_1_out));  // open: cin, cout
  and and_4 (CO, Q0, Q1, Q2, Q3);

  // Other names for the same wires on the sheet: CL = CLK
endmodule
