// Logisim project ficha6.circ as structural Verilog: 3 circuits, main circuit C74ls163
// ls163
module C74ls163 (
  input  ENP,
  input  ENT,
  input  LOAD_N,
  input  CLEAR_N,
  input  CLK,
  input  A,
  input  B,
  input  C,
  input  D,
  output CO,
  output Q0,
  output Q1,
  output Q2,
  output Q3
);

  wire and_1_out, and_2_out, not_1_out;
  wire [1:0] Sel;
  wire [3:0] adder_1_out, multiplexer_1_out;

  not not_1 (not_1_out, LOAD_N);
  Multiplexer #(.enable("false"), .select(2), .width(4)) multiplexer_1 (
    .in0(4'b0000), .in1({D, C, B, A}), .in2({Q3, Q2, Q1, Q0}), .in3(adder_1_out), .out(multiplexer_1_out),
    .sel(Sel));
  and and_1 (and_1_out, CLEAR_N, not_1_out);
  and and_2 (and_2_out, ENP, ENT, CLEAR_N);
  and and_3 (Sel[1], LOAD_N, CLEAR_N);
  Register #(.width(4)) register_1 (.D(multiplexer_1_out), .en(1'b1), .clk(CLK), .Q({Q3, Q2, Q1, Q0}));  // open: clr
  or or_1 (Sel[0], and_1_out, and_2_out);
  Adder #(.width(4)) adder_1 (.a({Q3, Q2, Q1, Q0}), .b(4'b0001), .out(adder_1_out));  // open: cin, cout
  and and_4 (CO, Q0, Q1, Q2, Q3);

  // Other names for the same wires on the sheet: CL = CLK
endmodule

module trabalho6 (
  input  in_1,
  input  in_2,
  input  in_3,
  input  in_4,
  input  in_5,
  input  in_6,
  input  in_7,
  output out_8
);

  wire c74ls163_1_q0, c74ls163_1_q1, c74ls163_1_q2, c74ls163_1_q3, clock_1_out, descodificador_1_p5,
       descodificador_1_p6, descodificador_1_p7, descodificador_1_p8, descodificador_1_p9,
       descodificador_1_p10, descodificador_1_p11, M, not_1_out, not_2_out;

  Clock clock_1 (.out(clock_1_out));
  nand nand_1 (M, c74ls163_1_q0, not_1_out, not_2_out, c74ls163_1_q3);
  C74ls163 c74ls163_1 (
    .Q0(c74ls163_1_q0), .Q1(c74ls163_1_q1), .Q2(c74ls163_1_q2), .Q3(c74ls163_1_q3), .CO(out_8),
    .CLK(clock_1_out), .ENP(in_1), .ENT(in_2), .LOAD_N(M), .CLEAR_N(in_3), .A(in_4), .B(in_5), .C(in_6),
    .D(in_7));
  not not_1 (not_1_out, c74ls163_1_q1);
  not not_2 (not_2_out, c74ls163_1_q2);
  // descodificador descodificador_1: pin names not known; wires that end beside it: c74ls163_1_q3, c74ls163_1_q2, c74ls163_1_q1, c74ls163_1_q0, descodificador_1_p5, descodificador_1_p6, descodificador_1_p7, descodificador_1_p8, descodificador_1_p9, descodificador_1_p10, descodificador_1_p11
  _7_Segment_Display u_7_segment_display_1 (
    .g(descodificador_1_p11), .f(descodificador_1_p10), .a(descodificador_1_p5), .b(descodificador_1_p6),
    .e(descodificador_1_p9), .d(descodificador_1_p8), .c(descodificador_1_p7));  // open: dp
endmodule

module contador (
  input  in_1,
  input  in_2,
  input  in_3,
  input  in_4,
  input  in_5,
  input  in_6,
  input  in_7,
  input  in_8,
  input  in_9,
  input  in_10,
  input  in_11,
  input  in_12,
  input  in_13,
  input  [7:0] in_14
);

  wire c74ls163_1_co, clock_1_out, ENP, M;
  wire [7:0] c74ls163_2_q0;

  Clock clock_1 (.out(clock_1_out));
  // Probe on 8'h7d
  nand nand_1 (M, ~c74ls163_2_q0[4], ~c74ls163_2_q0[5], ~c74ls163_2_q0[6], c74ls163_2_q0[7], c74ls163_2_q0[0], c74ls163_2_q0[1], c74ls163_2_q0[2], ~c74ls163_2_q0[3]);  // NAND_Gate
  C74ls163 c74ls163_1 (
    .Q0(c74ls163_2_q0[4]), .Q1(c74ls163_2_q0[5]), .Q2(c74ls163_2_q0[6]), .Q3(c74ls163_2_q0[7]),
    .CO(c74ls163_1_co), .CLK(clock_1_out), .ENP(ENP), .ENT(in_1), .LOAD_N(M), .CLEAR_N(in_2), .A(in_4),
    .B(in_6), .C(in_7), .D(in_9));
  // Probe on c74ls163_2_q0[7:4]
  // Probe on c74ls163_2_q0
  C74ls163 c74ls163_2 (
    .Q0(c74ls163_2_q0[0]), .Q1(c74ls163_2_q0[1]), .Q2(c74ls163_2_q0[2]), .Q3(c74ls163_2_q0[3]), .CO(ENP),
    .CLK(clock_1_out), .ENP(in_3), .ENT(in_5), .LOAD_N(M), .CLEAR_N(in_8), .A(in_10), .B(in_11), .C(in_12),
    .D(in_13));
  // Probe on c74ls163_2_q0[3:0]
endmodule
