// Logisim project ficha_1.circ as structural Verilog: 7 circuits, main circuit LS7400_PORTA_NAND
module LS7400_PORTA_NAND (
  input  _74LS00,
  input  in_2,
  output out_3
);

  nand nand_1 (out_3, _74LS00, in_2);

  // Notes on the sheet:
  //   NAND
endmodule

module LS7402_PORTA_NOR (
  input  in_1,
  input  in_2,
  output out_3
);

  nor nor_1 (out_3, in_1, in_2);

  // Notes on the sheet:
  //   LS7402 NOR
endmodule

module LS7404_PORTA_NOT (
  input  in_1,
  output out_2
);

  not not_1 (out_2, in_1);

  // Notes on the sheet:
  //   LS7404 NOT
endmodule

module LS7408_PORTA_AND (
  input  in_1,
  input  in_2,
  output out_3
);

  and and_1 (out_3, in_1, in_2);

  // Notes on the sheet:
  //   LS7408 AND
endmodule

module LS7432_PORTA_OR (
  input  in_1,
  input  in_2,
  output out_3
);

  or or_1 (out_3, in_1, in_2);

  // Notes on the sheet:
  //   LS7432 OR
endmodule

module LS7486_PORTA_OR (
  input  in_1,
  input  in_2,
  output out_3
);

  or or_1 (out_3, in_1, in_2);

  // Notes on the sheet:
  //   LS7486 OR
endmodule

module LS74266_PORTA_NOR (
  input  in_1,
  input  in_2,
  output out_3
);

  nor nor_1 (out_3, in_1, in_2);

  // Notes on the sheet:
  //   LS74266 NOR 
endmodule
