// Logisim project ficha_4.circ as structural Verilog: 4 circuits, main circuit main2
module main2 (
  input  b
);

  wire clock_1_out, contador_1_n0, contador_1_n1, contador_1_n2, d_ff_1_q, d_ff_2_q, d_ff_3_q,
       descodificador_1_a, descodificador_1_b, descodificador_1_c, descodificador_1_d, descodificador_1_e,
       descodificador_1_f, descodificador_1_g;

  D_Flip_Flop d_ff_1 (.D(contador_1_n2), .clk(clock_1_out), .Q(d_ff_1_q));  // open: Qn, preset, reset
  D_Flip_Flop d_ff_2 (.D(contador_1_n1), .clk(clock_1_out), .Q(d_ff_2_q));  // open: Qn, preset, reset
  Clock clock_1 (.out(clock_1_out));
  contador contador_1 (
    .s2(d_ff_1_q), .s1(d_ff_2_q), .s0(d_ff_3_q), .b(b), .n2(contador_1_n2), .n1(contador_1_n1),
    .n0(contador_1_n0));
  D_Flip_Flop d_ff_3 (.D(contador_1_n0), .clk(clock_1_out), .Q(d_ff_3_q));  // open: Qn, preset, reset
  descodificador descodificador_1 (
    .y(contador_1_n2), .z(contador_1_n1), .w(contador_1_n0), .a(descodificador_1_a), .f(descodificador_1_f),
    .b(descodificador_1_b), .g(descodificador_1_g), .e(descodificador_1_e), .c(descodificador_1_c),
    .d(descodificador_1_d));  // open: x
  _7_Segment_Display u_7_segment_display_1 (
    .g(descodificador_1_g), .f(descodificador_1_f), .a(descodificador_1_a), .b(descodificador_1_b),
    .e(descodificador_1_e), .d(descodificador_1_d), .c(descodificador_1_c));  // open: dp
endmodule

module maqest (
  input  s1,
  input  s01,
  input  b,
  output x,
  output n1,
  output n0
);

  wire and_1_out, and_2_out, and_3_out, and_4_out, not_1_out, not_2_out;

  not not_1 (not_1_out, s1);
  not not_2 (not_2_out, s01);
  or or_1 (x, s01, s1);
  and and_1 (and_1_out, not_1_out, s01);
  and and_2 (and_2_out, s1, not_2_out);
  and and_3 (and_3_out, not_2_out, b);
  and and_4 (and_4_out, s1, not_2_out);
  or or_2 (n1, and_1_out, and_2_out);
  or or_3 (n0, and_3_out, and_4_out);
endmodule

module contador (
  input  s2,
  input  s1,
  input  s0,
  input  b,
  output n2,
  output n1,
  output n0
);

  wire and_1_out, and_2_out, and_3_out, and_4_out, and_5_out, and_6_out, and_7_out, and_8_out, and_9_out,
       and_10_out, not_1_out, not_2_out, not_4_out;

  not not_1 (not_1_out, s2);
  not not_2 (not_2_out, s1);
  not not_3 (n0, s0);
  not not_4 (not_4_out, b);
  and and_1 (and_1_out, not_1_out, not_2_out, n0, not_4_out);
  and and_2 (and_2_out, not_1_out, s1, s0, b);
  and and_3 (and_3_out, s2, not_2_out, b);
  and and_4 (and_4_out, s2, not_2_out, s0);
  and and_5 (and_5_out, s2, s1, n0);
  and and_6 (and_6_out, s2, s1, not_4_out);
  and and_7 (and_7_out, not_2_out, n0, not_4_out);
  and and_8 (and_8_out, not_2_out, s0, b);
  and and_9 (and_9_out, s1, n0, b);
  and and_10 (and_10_out, s1, s0, not_4_out);
  or or_1 (n2, and_1_out, and_2_out, and_3_out, and_4_out, and_5_out, and_6_out);
  or or_2 (n1, and_7_out, and_8_out, and_9_out, and_10_out);
endmodule

module CONTADOR_EXT (
  input  Input_1,
  output AQ,
  output Output_1,
  output Output_2,
  output Output_3,
  output Output_4,
  output Output_5,
  output Output_6
);

  wire clock_1_out, contador_1_n0, contador_1_n1, contador_1_n2, d_ff_1_q, d_ff_2_q, d_ff_3_q;

  D_Flip_Flop d_ff_1 (.D(contador_1_n2), .clk(clock_1_out), .Q(d_ff_1_q));  // open: Qn, preset, reset
  D_Flip_Flop d_ff_2 (.D(contador_1_n1), .clk(clock_1_out), .Q(d_ff_2_q));  // open: Qn, preset, reset
  Clock clock_1 (.out(clock_1_out));
  contador contador_1 (
    .s2(d_ff_1_q), .s1(d_ff_2_q), .s0(d_ff_3_q), .b(Input_1), .n2(contador_1_n2), .n1(contador_1_n1),
    .n0(contador_1_n0));
  D_Flip_Flop d_ff_3 (.D(contador_1_n0), .clk(clock_1_out), .Q(d_ff_3_q));  // open: Qn, preset, reset
  descodificador descodificador_1 (
    .y(contador_1_n2), .z(contador_1_n1), .w(contador_1_n0), .a(AQ), .f(Output_1), .b(Output_2),
    .g(Output_3), .e(Output_4), .c(Output_5), .d(Output_6));  // open: x
endmodule
