// Logisim project martimvalente-bcd7seg.circ as structural Verilog: 18 circuits, main circuit main
module main (
  input  in_1,
  input  in_2,
  input  in_3,
  input  in_4,
  input  in_5,
  input  in_6,
  input  in_7,
  input  in_8
);

  wire descodificador_1_a, descodificador_1_b, descodificador_1_c, descodificador_1_d, descodificador_1_e,
       descodificador_1_f, descodificador_1_g, descodificadoranodo_1_a, descodificadoranodo_1_b,
       descodificadoranodo_1_c, descodificadoranodo_1_d, descodificadoranodo_1_e, descodificadoranodo_1_f,
       descodificadoranodo_1_g;

  descodificador descodificador_1 (
    .x(in_1), .y(in_2), .z(in_3), .w(in_4), .a(descodificador_1_a), .f(descodificador_1_f),
    .b(descodificador_1_b), .g(descodificador_1_g), .e(descodificador_1_e), .c(descodificador_1_c),
    .d(descodificador_1_d));
  descodificadorAnodo descodificadoranodo_1 (
    .x(in_5), .y(in_6), .z(in_7), .w(in_8), .a(descodificadoranodo_1_a), .f(descodificadoranodo_1_f),
    .b(descodificadoranodo_1_b), .g(descodificadoranodo_1_g), .e(descodificadoranodo_1_e),
    .c(descodificadoranodo_1_c), .d(descodificadoranodo_1_d));
  _7_Segment_Display u_7_segment_display_1 (
    .g(descodificador_1_g), .f(descodificador_1_f), .a(descodificador_1_a), .b(descodificador_1_b),
    .e(descodificador_1_e), .d(descodificador_1_d), .c(descodificador_1_c));  // open: dp
  _7_Segment_Display #(.active("false")) u_7_segment_display_2 (
    .g(descodificadoranodo_1_g), .f(descodificadoranodo_1_f), .a(descodificadoranodo_1_a),
    .b(descodificadoranodo_1_b), .e(descodificadoranodo_1_e), .d(descodificadoranodo_1_d),
    .c(descodificadoranodo_1_c));  // open: dp
endmodule

module segmentoA (
  input  x,
  input  y,
  input  z,
  input  w,
  output a
);

  wire and_1_out, and_2_out, and_3_out, and_4_out, and_5_out, and_6_out, not_1_out, not_2_out, not_3_out,
       not_4_out;

  not not_1 (not_1_out, x);
  not not_2 (not_2_out, y);
  not not_3 (not_3_out, z);
  not not_4 (not_4_out, w);
  and and_1 (and_1_out, not_2_out, not_4_out);
  and and_2 (and_2_out, not_1_out, z);
  and and_3 (and_3_out, not_1_out, y, w);
  and and_4 (and_4_out, y, z);
  and and_5 (and_5_out, x, not_2_out, not_3_out);
  and and_6 (and_6_out, x, not_4_out);
  or or_1 (a, and_1_out, and_2_out, and_3_out, and_4_out, and_5_out, and_6_out);
endmodule

module segmentoB (
  input  x,
  input  y,
  input  z,
  input  w,
  output b
);

  wire and_1_out, and_2_out, and_3_out, and_4_out, and_5_out, not_1_out, not_2_out, not_3_out, not_4_out;

  not not_1 (not_1_out, x);
  not not_2 (not_2_out, y);
  not not_3 (not_3_out, z);
  not not_4 (not_4_out, w);
  and and_1 (and_1_out, not_1_out, not_2_out);
  and and_2 (and_2_out, not_1_out, not_3_out, not_4_out);
  and and_3 (and_3_out, not_2_out, not_4_out);
  and and_4 (and_4_out, not_1_out, z, w);
  and and_5 (and_5_out, x, not_3_out, w);
  or or_1 (b, and_1_out, and_2_out, and_3_out, and_4_out, and_5_out);
endmodule

module segmentoC (
  input  x,
  input  y,
  input  z,
  input  w,
  output c
);

  wire and_1_out, and_2_out, and_3_out, and_4_out, and_5_out, not_1_out, not_2_out, not_3_out;

  not not_1 (not_1_out, x);
  not not_2 (not_2_out, y);
  not not_3 (not_3_out, z);
  and and_1 (and_1_out, not_1_out, not_3_out);
  and and_2 (and_2_out, not_1_out, w);
  and and_3 (and_3_out, not_3_out, w);
  and and_4 (and_4_out, not_1_out, y);
  and and_5 (and_5_out, x, not_2_out);
  or or_1 (c, and_1_out, and_2_out, and_3_out, and_4_out, and_5_out);
endmodule

module segmentoD (
  input  x,
  input  y,
  input  z,
  input  w,
  output d
);

  wire and_1_out, and_2_out, and_3_out, and_4_out, and_5_out, not_1_out, not_2_out, not_3_out, not_4_out;

  not not_1 (not_1_out, x);
  not not_2 (not_2_out, y);
  not not_3 (not_3_out, z);
  not not_4 (not_4_out, w);
  and and_1 (and_1_out, not_1_out, not_2_out, not_4_out);
  and and_2 (and_2_out, not_2_out, z, w);
  and and_3 (and_3_out, y, not_3_out, w);
  and and_4 (and_4_out, y, z, not_4_out);
  and and_5 (and_5_out, x, not_3_out, not_4_out);
  or or_1 (d, and_1_out, and_2_out, and_3_out, and_4_out, and_5_out);
endmodule

module sgE (
  input  x,
  input  y,
  input  z,
  input  w,
  output e
);

  wire and_1_out, and_2_out, and_3_out, and_4_out, not_1_out, not_2_out;

  not not_1 (not_1_out, y);
  not not_2 (not_2_out, w);
  and and_1 (and_1_out, not_1_out, not_2_out);
  and and_2 (and_2_out, z, not_2_out);
  and and_3 (and_3_out, x, z);
  and and_4 (and_4_out, x, y);
  or or_1 (e, and_1_out, and_2_out, and_3_out, and_4_out);
endmodule

module sgF (
  input  x,
  input  y,
  input  z,
  input  w,
  output f
);

  wire and_1_out, and_2_out, and_3_out, and_4_out, and_5_out, not_1_out, not_2_out, not_3_out, not_4_out;

  not not_1 (not_1_out, x);
  not not_2 (not_2_out, y);
  not not_3 (not_3_out, z);
  not not_4 (not_4_out, w);
  and and_1 (and_1_out, not_3_out, not_4_out);
  and and_2 (and_2_out, not_1_out, y, not_3_out);
  and and_3 (and_3_out, y, not_4_out);
  and and_4 (and_4_out, x, not_2_out);
  and and_5 (and_5_out, x, z);
  or or_1 (f, and_1_out, and_2_out, and_3_out, and_4_out, and_5_out);
endmodule

module sgG (
  input  x,
  input  y,
  input  z,
  input  w,
  output g
);

  wire and_1_out, and_2_out, and_3_out, and_4_out, and_5_out, not_1_out, not_2_out, not_3_out, not_4_out;

  not not_1 (not_1_out, x);
  not not_2 (not_2_out, y);
  not not_3 (not_3_out, z);
  not not_4 (not_4_out, w);
  and and_1 (and_1_out, not_2_out, z);
  and and_2 (and_2_out, z, not_4_out);
  and and_3 (and_3_out, not_1_out, y, not_3_out);
  and and_4 (and_4_out, x, not_2_out);
  and and_5 (and_5_out, x, w);
  or or_1 (g, and_1_out, and_2_out, and_3_out, and_4_out, and_5_out);
endmodule

module sgDP (
  input  x,
  input  y,
  input  z,
  input  w,
  output dp
);


  assign dp = 1'b0;
endmodule

module descodificador (
  input  x,
  input  y,
  input  z,
  input  w,
  output a,
  output f,
  output b,
  output g,
  output e,
  output c,
  output d
);

  segmentoA segmentoa_1 (.x(x), .y(y), .z(z), .w(w), .a(a));
  segmentoB segmentob_1 (.x(x), .y(y), .z(z), .w(w), .b(b));
  segmentoC segmentoc_1 (.x(x), .y(y), .z(z), .w(w), .c(c));
  segmentoD segmentod_1 (.x(x), .y(y), .z(z), .w(w), .d(d));
  sgE sge_1 (.x(x), .y(y), .z(z), .w(w), .e(e));
  sgF sgf_1 (.x(x), .y(y), .z(z), .w(w), .f(f));
  sgG sgg_1 (.x(x), .y(y), .z(z), .w(w), .g(g));
  sgDP sgdp_1 (.x(x), .y(y), .z(z), .w(w));  // open: dp
endmodule

module ansgA (
  input  x,
  input  y,
  input  z,
  input  w,
  output a
);

  wire and_1_out, and_2_out, and_3_out, and_4_out, not_1_out, not_2_out, not_3_out, not_4_out;

  not not_1 (not_1_out, x);
  not not_2 (not_2_out, y);
  not not_3 (not_3_out, z);
  not not_4 (not_4_out, w);
  and and_1 (and_1_out, not_1_out, not_2_out, not_3_out, w);
  and and_2 (and_2_out, not_1_out, y, not_3_out, not_4_out);
  and and_3 (and_3_out, x, not_2_out, z, w);
  and and_4 (and_4_out, x, y, not_3_out, w);
  or or_1 (a, and_1_out, and_2_out, and_3_out, and_4_out);
endmodule

module ansgB (
  input  x,
  input  y,
  input  z,
  input  w,
  output b
);

  wire and_1_out, and_2_out, and_3_out, and_4_out, not_1_out, not_2_out, not_3_out;

  not not_1 (not_1_out, x);
  not not_2 (not_2_out, z);
  not not_3 (not_3_out, w);
  and and_1 (and_1_out, not_1_out, y, not_2_out, w);
  and and_2 (and_2_out, y, z, not_3_out);
  and and_3 (and_3_out, x, z, w);
  and and_4 (and_4_out, x, y, not_3_out);
  or or_1 (b, and_1_out, and_2_out, and_3_out, and_4_out);
endmodule

module ansgC (
  input  x,
  input  y,
  input  z,
  input  w,
  output c
);

  wire and_1_out, and_2_out, and_3_out, not_1_out, not_2_out, not_3_out;

  not not_1 (not_1_out, x);
  not not_2 (not_2_out, y);
  not not_3 (not_3_out, w);
  and and_1 (and_1_out, not_1_out, not_2_out, z, not_3_out);
  and and_2 (and_2_out, x, y, not_3_out);
  and and_3 (and_3_out, x, y, z);
  or or_1 (c, and_1_out, and_2_out, and_3_out);
endmodule

module ansgD (
  input  x,
  input  y,
  input  z,
  input  w,
  output d
);

  wire and_1_out, and_2_out, and_3_out, and_4_out, not_1_out, not_2_out, not_3_out, not_4_out;

  not not_1 (not_1_out, x);
  not not_2 (not_2_out, y);
  not not_3 (not_3_out, z);
  not not_4 (not_4_out, w);
  and and_1 (and_1_out, not_2_out, not_3_out, w);
  and and_2 (and_2_out, not_1_out, y, not_3_out, not_4_out);
  and and_3 (and_3_out, y, z, w);
  and and_4 (and_4_out, x, not_2_out, z, not_4_out);
  or or_1 (d, and_1_out, and_2_out, and_3_out, and_4_out);
endmodule

module ansgE (
  input  x,
  input  y,
  input  z,
  input  w,
  output e
);

  wire and_1_out, and_2_out, and_3_out, not_1_out, not_2_out, not_3_out;

  not not_1 (not_1_out, x);
  not not_2 (not_2_out, y);
  not not_3 (not_3_out, z);
  and and_1 (and_1_out, not_1_out, w);
  and and_2 (and_2_out, not_2_out, not_3_out, w);
  and and_3 (and_3_out, not_1_out, y, not_3_out);
  or or_1 (e, and_1_out, and_2_out, and_3_out);
endmodule

module ansgF (
  input  x,
  input  y,
  input  z,
  input  w,
  output f
);

  wire and_1_out, and_2_out, and_3_out, and_4_out, not_1_out, not_2_out, not_3_out;

  not not_1 (not_1_out, x);
  not not_2 (not_2_out, y);
  not not_3 (not_3_out, z);
  and and_1 (and_1_out, not_1_out, not_2_out, w);
  and and_2 (and_2_out, not_1_out, not_2_out, z);
  and and_3 (and_3_out, not_1_out, z, w);
  and and_4 (and_4_out, x, y, not_3_out, w);
  or or_1 (f, and_1_out, and_2_out, and_3_out, and_4_out);
endmodule

module ansgG (
  input  x,
  input  y,
  input  z,
  input  w,
  output g
);

  wire and_1_out, and_2_out, and_3_out, not_1_out, not_2_out, not_3_out, not_4_out;

  not not_1 (not_1_out, x);
  not not_2 (not_2_out, y);
  not not_3 (not_3_out, z);
  not not_4 (not_4_out, w);
  and and_1 (and_1_out, not_1_out, not_2_out, not_3_out);
  and and_2 (and_2_out, not_1_out, y, z, w);
  and and_3 (and_3_out, x, y, not_3_out, not_4_out);
  or or_1 (g, and_1_out, and_2_out, and_3_out);
endmodule

module descodificadorAnodo (
  input  x,
  input  y,
  input  z,
  input  w,
  output a,
  output f,
  output b,
  output g,
  output e,
  output c,
  output d
);

  ansgA ansga_1 (.x(x), .y(y), .z(z), .w(w), .a(a));
  ansgB ansgb_1 (.x(x), .y(y), .z(z), .w(w), .b(b));
  ansgC ansgc_1 (.x(x), .y(y), .z(z), .w(w), .c(c));
  ansgD ansgd_1 (.x(x), .y(y), .z(z), .w(w), .d(d));
  ansgE ansge_1 (.x(x), .y(y), .z(z), .w(w), .e(e));
  ansgF ansgf_1 (.x(x), .y(y), .z(z), .w(w), .f(f));
  ansgG ansgg_1 (.x(x), .y(y), .z(z), .w(w), .g(g));
endmodule
